// Logisim project cpu21-riscv.circ as structural Verilog: 17 circuits, main circuit ◇单周期RISC-V
module \单周期RISC_V  (
  input  IR1,
  input  IR2,
  input  IR3,
  output RegWrite,
  output MemWrite,
  output [31:0] PC,
  output [31:0] IR,
  output [31:0] RDin,
  output [31:0] MDin,
  output [31:0] LedData
);

  wire alu_1_equal, alu_1_out_6, and_1_out, and_2_out, and_3_out, and_4_out, and_5_out, CLK, clock_1_out,
       comparator_1_eq, comparator_2_eq, comparator_2_lt, d_ff_1_q, ecall, Go, halt, IR1_t, IR2_t, IR3_t,
       IRA, IRB, IRC, nand_1_out, not_1_out, not_2_out, not_3_out, not_4_out, or_3_out, riscv_probe_1_p2,
       RST, W1, W2, W3, \单周期硬布线控制器_1_beq , \单周期硬布线控制器_1_bltu , \单周期硬布线控制器_1_bne , \单周期硬布线控制器_1_jal ,
       \单周期硬布线控制器_1_jalr ;
  wire [1:0] priority_encoder_1_out, \单周期硬布线控制器_1_memtoreg , \单周期硬布线控制器_1_s_type ;
  wire [3:0] \单周期硬布线控制器_1_alu_op ;
  wire [4:0] multiplexer_2_out, multiplexer_3_out;
  wire [12:0] CNT_num;
  wire [15:0] \总周期数 ;
  wire [31:0] adder_2_out, adder_3_out, alu_1_result, bit_extender_1_out, bit_extender_2_out,
       bit_extender_3_out, bit_extender_4_out, multiplexer_1_out, multiplexer_4_out, multiplexer_5_out, PC_4,
       ram_1_data, regifile_1_r1, shifter_1_out, shifter_2_out;

  Button \u_继续运行  (.out(Go));
  Button _1 (.out(IRA));
  Button _2 (.out(IRB));
  Button _3 (.out(IRC));
  LED #(.active("true")) led_1 (.in(W1));
  LED #(.active("true")) led_2 (.in(W2));
  LED #(.active("true")) led_3 (.in(W3));
  Hex_Digit_Display hex_digit_display_1 (.value(LedData[31:28]));  // open: dp
  Hex_Digit_Display hex_digit_display_2 (.value(LedData[27:24]));  // open: dp
  Hex_Digit_Display hex_digit_display_3 (.value(LedData[23:20]));  // open: dp
  Priority_Encoder #(.select(2), .disabled("Z")) priority_encoder_1 (
    .in0(1'b1), .in1(\单周期硬布线控制器_1_jalr ), .in2(\单周期硬布线控制器_1_jal ), .in3(or_3_out),
    .out(priority_encoder_1_out));  // open: gs, en_out, en_in
  Multiplexer #(.select(2), .width(32), .disabled("Z"), .enable("false")) multiplexer_1 (
    .in0(PC_4), .in1(alu_1_result), .in2(adder_3_out), .in3(adder_2_out), .out(multiplexer_1_out),
    .sel(priority_encoder_1_out));
  Hex_Digit_Display hex_digit_display_4 (.value(LedData[15:12]));  // open: dp
  Hex_Digit_Display hex_digit_display_5 (.value(LedData[19:16]));  // open: dp
  Register #(.width(32), .trigger("rising"), .Select("low")) u_PC (
    .D(multiplexer_1_out), .en(not_1_out), .Q(PC), .clk(CLK), .clr(RST));
  not not_1 (not_1_out, halt);
  Hex_Digit_Display hex_digit_display_6 (.value(LedData[7:4]));  // open: dp
  Hex_Digit_Display hex_digit_display_7 (.value(LedData[11:8]));  // open: dp
  // Probe on \总周期数 
  Hex_Digit_Display hex_digit_display_8 (.value(LedData[3:0]));  // open: dp
  // RiscV_Probe riscv_probe_1: pin names not known; wires that end beside it: IR, riscv_probe_1_p2
  ROM #(.addrWidth(10), .dataWidth(32), .Select("high")) rom_1 (.addr(PC[11:2]), .data(IR));
  Adder #(.width(32)) adder_1 (.a(PC), .b(32'h4), .out(PC_4));  // open: cin, cout
  or or_1 (IR1_t, IR1, IRA);
  or or_2 (IR2_t, IR2, IRB);
  or or_3 (or_3_out, and_3_out, and_1_out, and_2_out);
  \单周期硬布线控制器  \u_单周期硬布线控制器_1  (
    .Funct({IR[30], IR[25], IR[14:12]}), .OP(IR[6:2]), .ALU_OP(\单周期硬布线控制器_1_alu_op ),
    .MemToReg(\单周期硬布线控制器_1_memtoreg [0]), .MemWrite(MemWrite), .ALU_SRC(riscv_probe_1_p2),
    .RegWrite(RegWrite), .ecall(ecall), .S_type(\单周期硬布线控制器_1_s_type [0]), .Jalr(\单周期硬布线控制器_1_jalr ),
    .Beq(\单周期硬布线控制器_1_beq ), .JAL(\单周期硬布线控制器_1_jal ), .Bne(\单周期硬布线控制器_1_bne ), .in_3(IR[21]),
    .U_Type(\单周期硬布线控制器_1_s_type [1]), .BLTU(\单周期硬布线控制器_1_bltu ));  // open: uret
  Multiplexer #(.select(1), .width(5), .disabled("Z"), .enable("false")) multiplexer_2 (
    .in0(IR[19:15]), .in1(5'b10001), .out(multiplexer_2_out), .sel(ecall));
  Multiplexer #(.select(1), .width(5), .disabled("Z"), .enable("false")) multiplexer_3 (
    .in0(IR[24:20]), .in1(5'b01010), .out(multiplexer_3_out), .sel(ecall));
  assign bit_extender_1_out = {{20{IR[31]}}, IR[31:20]};  // Bit_Extender bit_extender_1
  assign bit_extender_2_out = {{20{IR[31]}}, {IR[31:25], IR[11:7]}};  // Bit_Extender bit_extender_2
  and and_1 (and_1_out, \单周期硬布线控制器_1_bne , not_2_out);
  and and_2 (and_2_out, \单周期硬布线控制器_1_beq , alu_1_equal);
  Multiplexer #(.select(2), .width(32), .disabled("Z"), .enable("false")) multiplexer_4 (
    .in0(bit_extender_1_out), .in1(bit_extender_2_out), .in2({IR[31:12], {12{1'b0}}}),
    .out(multiplexer_4_out), .sel(\单周期硬布线控制器_1_s_type ));  // open: in3
  assign bit_extender_3_out = {{20{IR[31]}}, {IR[31], IR[7], IR[30:25], IR[11:8]}};  // Bit_Extender bit_extender_3
  assign bit_extender_4_out = {{12{IR[31]}}, {IR[31], IR[19:12], IR[20], IR[30:21]}};  // Bit_Extender bit_extender_4
  or or_4 (IR3_t, IR3, IRC);
  and and_3 (and_3_out, \单周期硬布线控制器_1_bltu , alu_1_out_6);
  not not_2 (not_2_out, alu_1_equal);
  Shifter #(.width(32), .shift("ll")) shifter_1 (.in(bit_extender_3_out), .\dist (5'b00001), .out(shifter_1_out));
  Shifter #(.width(32), .shift("ll")) shifter_2 (.in(bit_extender_4_out), .\dist (5'b00001), .out(shifter_2_out));
  Regifile regifile_1 (
    .Din(RDin), .Clk(CLK), .R1(regifile_1_r1), .R2(MDin), .WE(RegWrite), .W_num(IR[11:7]),
    .R1_num(multiplexer_2_out), .R2_num(multiplexer_3_out));
  Adder #(.width(32)) adder_2 (.a(shifter_1_out), .b(PC), .out(adder_2_out));  // open: cin, cout
  Adder #(.width(32)) adder_3 (.a(shifter_2_out), .b(PC), .out(adder_3_out));  // open: cin, cout
  Multiplexer #(.select(1), .width(32), .disabled("Z"), .enable("false")) multiplexer_5 (
    .in0(MDin), .in1(multiplexer_4_out), .out(multiplexer_5_out), .sel(riscv_probe_1_p2));
  ALU alu_1 (
    .X(regifile_1_r1), .Y(multiplexer_5_out), .AluOP(\单周期硬布线控制器_1_alu_op ), .Equal(alu_1_equal),
    .Result(alu_1_result), .out_6(alu_1_out_6));  // open: Result_2, out_4
  RAM #(.addrWidth(10), .dataWidth(32), .bus("separate"), .Select("high")) ram_1 (
    .addr(alu_1_result[11:2]), .din(MDin), .data(ram_1_data), .str(MemWrite), .sel(1'b1), .clk(CLK), .ld(1'b1));  // open: clr
  Comparator #(.width(32), .mode("twosComplement")) comparator_1 (
    .a(regifile_1_r1), .b(32'h22), .eq(comparator_1_eq));  // open: gt, lt
  not not_3 (not_3_out, halt);
  Counter #(.width(16), .max('hffff), .ongoal("wrap"), .trigger("rising"), .behavior("new")) counter_1 (
    .count(not_3_out), .Q(\总周期数 ), .clk(CLK));  // open: load, D, carry, clr, preset, down
  and and_4 (and_4_out, comparator_1_eq, ecall);
  not not_4 (not_4_out, comparator_1_eq);
  and and_5 (and_5_out, not_4_out, ecall);
  D_Flip_Flop #(.trigger("high"), .Pre_Clr_Positions("LEGACY"), .NegatePresetClear("false"), .enable("true"), .NewFFLayout("false")) d_ff_1 (.Q(d_ff_1_q));  // open: clk, D, Qn, preset, en, reset
  // Probe on 13'ha
  or or_5 (\单周期硬布线控制器_1_memtoreg [1], \单周期硬布线控制器_1_jal , \单周期硬布线控制器_1_jalr );
  Multiplexer #(.select(2), .width(32), .disabled("Z"), .enable("false")) multiplexer_6 (
    .in0(alu_1_result), .in1(ram_1_data), .in2(PC_4), .out(RDin), .sel(\单周期硬布线控制器_1_memtoreg ));  // open: in3
  Register #(.width(32), .trigger("rising"), .Select("low")) register_1 (
    .D(MDin), .en(and_4_out), .Q(LedData), .clk(CLK));  // open: clr
  Multiplexer #(.select(1), .width(1), .disabled("Z"), .enable("false")) multiplexer_7 (
    .in0(and_5_out), .in1(1'b0), .out(halt), .sel(Go));
  Comparator #(.width(13), .mode("twosComplement")) comparator_2 (
    .a(CNT_num), .b(13'ha), .eq(comparator_2_eq), .lt(comparator_2_lt));  // open: gt
  Clock #(.highDuration(1), .lowDuration(1)) clock_1 (.out(clock_1_out));
  Counter #(.width(13), .max('h1fff), .ongoal("stay"), .trigger("rising"), .behavior("old")) counter_2 (
    .count(comparator_2_lt), .Q(CNT_num), .clk(clock_1_out));  // open: load, D, carry, clr, preset
  nand nand_1 (nand_1_out, d_ff_1_q, comparator_2_eq);
  assign CLK = nand_1_out ? clock_1_out : 1'bz;  // Controlled_Buffer controlled_buffer_1
  Pull_Resistor #(.pull(1)) pull_resistor_1 (.node(CLK));

  // Notes on the sheet:
  //   中断源
  //   中断等待指示
  //   J
  //   B
  //   数码管输出应该用寄存器锁存，否则显示数据只能一闪而过
  //   ALU
  //   BranchAddress
  //   PCsrc
  //   数码管输出
  //   PC
  //   指令探针
  //   指令存储器
  //   指令字
  //   contents of rom_1 (hex, n*v repeats v):
  //   100493 100006f 100493 200913 300993 100006f 100493 200913 300993 100006f 100493 200913 300993
  //   100006f 100493 200913 300993 29c000ef 100413 100493 1f49493 900533 2200893 73 24d493 48463 fedff06f
  //   900533 2200893 73 100493 249493 900533 2200893 73 48463 fedff06f 100493 1f49493 900533 2200893 73
  //   4034d493 900533 2200893 73 4044d493 900533 2200893 73 4044d493 900533 2200893 73 4044d493 900533
  //   2200893 73 4044d493 900533 2200893 73 4044d493 900533 2200893 73 4044d493 900533 2200893 73 4044d493
  //   900533 2200893 73 100413 1f41993 41f9d993 433 c00913 300b13 140413 f47413 800293 100313 499993
  //   89e9b3 1300533 2200893 73 406282b3 fe0294e3 140413 f00f93 1f47433 1c41413 800293 100313 49d993
  //   89e9b3 1300533 2200893 73 406282b3 fe0294e3 1c45413 406b0b33 b0463 f95ff06f 2b3 fff2c293 829293
  //   ff2e293 500533 2200893 73 fff00413 493 84a023 140413 448493 84a023 140413 448493 84a023 140413
  //   448493 84a023 140413 448493 84a023 140413 448493 84a023 140413 448493 84a023 140413 448493 84a023
  //   140413 448493 84a023 140413 448493 84a023 140413 448493 84a023 140413 448493 84a023 140413 448493
  //   84a023 140413 448493 84a023 140413 448493 84a023 140413 448493 84a023 140413 448493 140413 433
  //   3c00493 42983 4aa03 149a2b3 28663 134a023 1442023 ffc48493 fe9412e3 800533 2200893 73 440413 3c00493
  //   fc9416e3 a00893 73 413 140413 800533 2200893 73 240413 800533 2200893 73 340413 800533 2200893 73
  //   440413 800533 2200893 73 540413 800533 2200893 73 640413 800533 2200893 73 740413 800533 2200893 73
  //   840413 800533 2200893 2200893 73 8067
  //   JAL
  //   JALR
  //   URET
  //   rs1
  //   shamt / rs2
  //   rd / B:imm[4:1|11]
  //   I
  //   S
  //   *U:imm[31:12]
  //   Beq
  //   Bne
  //   BLTU
  //   AluOP
  //   AluSrcB
  //   U_type
  //   S_type
  //   B:imm[12:0]
  //   J:imm[20:0]
  //   MemToReg
  //   MemWrite
  //   RegWrite
  //   PC
  //   EQU
  //   BranchAddress
  //   为方便自动评测，需要输出PC，IR，寄存器堆写如数据RDin
  //   RAM写使能MemWrite、RAM写入数据MDin等信号
  //   数据存储器
  //   R1
  //   MemToReg
  //   WriteBackData
  //   控制位
  //   暂停节拍，不能为0
  //   JAL or JALR
  //   R2
  //   戳工具置1进入计数暂停模式，ctrl+k时钟自动运行到对应节拍暂停
  //   ctrl+k关闭时钟连续运行，将控制位置零，进入单步调试模式调试
  //   用这个时钟源需要去掉电路中的其他时钟源
  //   可计数暂停的时钟源
endmodule

// 单周期硬布线控制器
module \单周期硬布线控制器  (
  input  [4:0] OP,
  input  [4:0] Funct,
  input  in_3,
  output [3:0] ALU_OP,
  output uret,
  output MemToReg,
  output U_Type,
  output ecall,
  output MemWrite,
  output ALU_SRC,
  output RegWrite,
  output S_type,
  output Beq,
  output Bne,
  output BLTU,
  output Jalr,
  output JAL
);

  wire \控制信号自动生成_1_ecall ;

  \运算控制器自动生成  \u_运算控制器自动生成_1  (
    .OP2(OP[0]), .OP3(OP[1]), .OP4(OP[2]), .OP5(OP[3]), .OP6(OP[4]), .F12(Funct[0]), .F13(Funct[1]),
    .F14(Funct[2]), .F25(Funct[3]), .F30(Funct[4]), .S0(ALU_OP[0]), .S1(ALU_OP[1]), .S2(ALU_OP[2]),
    .S3(ALU_OP[3]));
  \控制信号自动生成  \u_控制信号自动生成_1  (
    .OP2(OP[0]), .OP3(OP[1]), .MemToReg(MemToReg), .OP4(OP[2]), .OP5(OP[3]), .OP6(OP[4]), .U_Type(U_Type),
    .F12(Funct[0]), .F13(Funct[1]), .F14(Funct[2]), .F25(Funct[3]), .F30(Funct[4]), .MemWrite(MemWrite),
    .ALU_SRC(ALU_SRC), .RegWrite(RegWrite), .ecall(\控制信号自动生成_1_ecall ), .S_Type(S_type), .BEQ(Beq),
    .BNE(Bne), .BLTU(BLTU), .JALR(Jalr), .JAL(JAL));
  and and_1 (uret, in_3, \控制信号自动生成_1_ecall );
  and and_2 (ecall, ~in_3, \控制信号自动生成_1_ecall );  // AND_Gate

  // Other names for the same wires on the sheet: IR21 = in_3; OP_CODE[4:0] = OP

  // Notes on the sheet:
  //   运算器控制器，根据指令生成运算器功能选择信号
  //   控制信号生成，产生数据通路需要的其他控制信号
endmodule

// 运算器控制器
module \运算控制器自动生成  (
  input  OP2,
  input  OP3,
  input  OP4,
  input  OP5,
  input  OP6,
  input  F12,
  input  F13,
  input  F14,
  input  F25,
  input  F30,
  output S0,
  output S1,
  output S2,
  output S3
);

  wire and_1_out, and_2_out, and_3_out, and_4_out, and_5_out, and_6_out, and_7_out, and_8_out, and_9_out,
       and_10_out, and_11_out, and_12_out, and_13_out, and_14_out, and_15_out, and_16_out, and_17_out,
       and_18_out, and_19_out, and_20_out, and_21_out, and_22_out, and_23_out, and_24_out, and_25_out,
       and_26_out, and_27_out, and_28_out, and_29_out, and_30_out, and_31_out, and_32_out, and_33_out,
       and_34_out, and_35_out, and_36_out, and_37_out, and_38_out, and_39_out, and_40_out, and_41_out,
       not_1_out, not_2_out, not_3_out, not_4_out, not_5_out, not_6_out, not_7_out, not_8_out, not_9_out,
       not_10_out, not_11_out, not_12_out, not_13_out, not_14_out, not_15_out, not_16_out, not_17_out,
       not_18_out, not_19_out, not_20_out, not_21_out, not_22_out, not_23_out, not_24_out, not_25_out,
       not_26_out, not_27_out, not_28_out, not_29_out, not_30_out, not_31_out, not_32_out, not_33_out,
       not_34_out, not_35_out, not_36_out, not_37_out, not_38_out, not_39_out, not_40_out, not_41_out,
       not_42_out, not_43_out, not_44_out, not_45_out, not_46_out, not_47_out, not_48_out, not_49_out,
       not_50_out, not_51_out, not_52_out, not_53_out, not_54_out, not_55_out, not_56_out, not_57_out,
       not_58_out, not_59_out, not_60_out, not_61_out, not_62_out, not_63_out, not_64_out, not_65_out,
       not_66_out, not_67_out, not_68_out, not_69_out, not_70_out, not_71_out, not_72_out, not_73_out,
       not_74_out, not_75_out, not_76_out, not_77_out, not_78_out, not_79_out, not_80_out, not_81_out,
       not_82_out, not_83_out, not_84_out, not_85_out, not_86_out, not_87_out, not_88_out, not_89_out,
       not_90_out, not_91_out, not_92_out, not_93_out, not_94_out, not_95_out, not_96_out, not_97_out,
       not_98_out, not_99_out, not_100_out, not_101_out, not_102_out, not_103_out, not_104_out, not_105_out,
       not_106_out, not_107_out, not_108_out, not_109_out, not_110_out, not_111_out, not_112_out,
       not_113_out, not_114_out, not_115_out, not_116_out, not_117_out, not_118_out, not_119_out,
       not_120_out, not_121_out, not_122_out, not_123_out, not_124_out, not_125_out, not_126_out,
       not_127_out, not_128_out, not_129_out, not_130_out, not_131_out, not_132_out, not_133_out,
       not_134_out, not_135_out, not_136_out, not_137_out, not_138_out, not_139_out, not_140_out,
       not_141_out, not_142_out, not_143_out, not_144_out, not_145_out, not_146_out, not_147_out,
       not_148_out, not_149_out, not_150_out, not_151_out, not_152_out, not_153_out, not_154_out,
       not_155_out, not_156_out, not_157_out, not_158_out, not_159_out, not_160_out, not_161_out,
       not_162_out, not_163_out, not_164_out, not_165_out, not_166_out, not_167_out, not_168_out,
       not_169_out, not_170_out, not_171_out, not_172_out, not_173_out, not_174_out, not_175_out,
       not_176_out, not_177_out, not_178_out, not_179_out, not_180_out, not_181_out, not_182_out,
       not_183_out, not_184_out, not_185_out, not_186_out, not_187_out, not_188_out, not_189_out,
       not_190_out, not_191_out, not_192_out, not_193_out, not_194_out, not_195_out, not_196_out,
       not_197_out, not_198_out, not_199_out, not_200_out, not_201_out, not_202_out, not_203_out,
       not_204_out, not_205_out, not_206_out, not_207_out, not_208_out, not_209_out, not_210_out,
       not_211_out, not_212_out, not_213_out, not_214_out, not_215_out, not_216_out, not_217_out,
       not_218_out, not_219_out, not_220_out, not_221_out, not_222_out, not_223_out, not_224_out,
       not_225_out, not_226_out, not_227_out, not_228_out, not_229_out, not_230_out, not_231_out,
       not_232_out, not_233_out, not_234_out, not_235_out, not_236_out, not_237_out, not_238_out,
       not_239_out, not_240_out, not_241_out, not_242_out;

  not not_1 (not_1_out, F30);
  not not_2 (not_2_out, F25);
  not not_3 (not_3_out, F14);
  not not_4 (not_4_out, F13);
  not not_5 (not_5_out, F12);
  not not_6 (not_6_out, OP6);
  not not_7 (not_7_out, OP3);
  not not_8 (not_8_out, OP2);
  not not_9 (not_9_out, F30);
  not not_10 (not_10_out, F25);
  not not_11 (not_11_out, OP6);
  not not_12 (not_12_out, OP3);
  not not_13 (not_13_out, OP2);
  not not_14 (not_14_out, F30);
  not not_15 (not_15_out, F25);
  not not_16 (not_16_out, F14);
  not not_17 (not_17_out, F12);
  not not_18 (not_18_out, OP6);
  not not_19 (not_19_out, OP3);
  not not_20 (not_20_out, OP2);
  not not_21 (not_21_out, F14);
  not not_22 (not_22_out, F13);
  not not_23 (not_23_out, F12);
  not not_24 (not_24_out, OP6);
  not not_25 (not_25_out, OP5);
  not not_26 (not_26_out, OP3);
  not not_27 (not_27_out, OP2);
  not not_28 (not_28_out, OP6);
  not not_29 (not_29_out, OP5);
  not not_30 (not_30_out, OP3);
  not not_31 (not_31_out, OP2);
  not not_32 (not_32_out, F13);
  not not_33 (not_33_out, F12);
  not not_34 (not_34_out, OP6);
  not not_35 (not_35_out, OP5);
  not not_36 (not_36_out, OP3);
  not not_37 (not_37_out, OP2);
  not not_38 (not_38_out, F14);
  not not_39 (not_39_out, F12);
  not not_40 (not_40_out, OP6);
  not not_41 (not_41_out, OP5);
  not not_42 (not_42_out, OP3);
  not not_43 (not_43_out, OP2);
  not not_44 (not_44_out, F25);
  not not_45 (not_45_out, F13);
  not not_46 (not_46_out, OP6);
  not not_47 (not_47_out, OP5);
  not not_48 (not_48_out, OP3);
  not not_49 (not_49_out, OP2);
  not not_50 (not_50_out, F14);
  not not_51 (not_51_out, F12);
  not not_52 (not_52_out, OP6);
  not not_53 (not_53_out, OP5);
  not not_54 (not_54_out, OP4);
  not not_55 (not_55_out, OP3);
  not not_56 (not_56_out, OP2);
  not not_57 (not_57_out, F14);
  not not_58 (not_58_out, F12);
  not not_59 (not_59_out, OP6);
  not not_60 (not_60_out, OP4);
  not not_61 (not_61_out, OP3);
  not not_62 (not_62_out, OP2);
  not not_63 (not_63_out, F14);
  not not_64 (not_64_out, F13);
  not not_65 (not_65_out, OP6);
  not not_66 (not_66_out, OP4);
  not not_67 (not_67_out, OP3);
  not not_68 (not_68_out, OP2);
  not not_69 (not_69_out, F25);
  not not_70 (not_70_out, F14);
  not not_71 (not_71_out, F13);
  not not_72 (not_72_out, F12);
  not not_73 (not_73_out, OP6);
  not not_74 (not_74_out, OP3);
  not not_75 (not_75_out, OP2);
  not not_76 (not_76_out, F30);
  not not_77 (not_77_out, F25);
  not not_78 (not_78_out, OP6);
  not not_79 (not_79_out, OP3);
  not not_80 (not_80_out, OP2);
  not not_81 (not_81_out, F30);
  not not_82 (not_82_out, F25);
  not not_83 (not_83_out, F14);
  not not_84 (not_84_out, F12);
  not not_85 (not_85_out, OP6);
  not not_86 (not_86_out, OP3);
  not not_87 (not_87_out, OP2);
  not not_88 (not_88_out, OP6);
  not not_89 (not_89_out, OP5);
  not not_90 (not_90_out, OP3);
  not not_91 (not_91_out, OP2);
  not not_92 (not_92_out, F14);
  not not_93 (not_93_out, F12);
  not not_94 (not_94_out, OP6);
  not not_95 (not_95_out, OP5);
  not not_96 (not_96_out, OP3);
  not not_97 (not_97_out, OP2);
  not not_98 (not_98_out, F30);
  not not_99 (not_99_out, F25);
  not not_100 (not_100_out, F13);
  not not_101 (not_101_out, OP6);
  not not_102 (not_102_out, OP5);
  not not_103 (not_103_out, OP3);
  not not_104 (not_104_out, OP2);
  not not_105 (not_105_out, F14);
  not not_106 (not_106_out, F13);
  not not_107 (not_107_out, F12);
  not not_108 (not_108_out, OP4);
  not not_109 (not_109_out, OP3);
  not not_110 (not_110_out, OP2);
  not not_111 (not_111_out, F14);
  not not_112 (not_112_out, F13);
  not not_113 (not_113_out, OP4);
  not not_114 (not_114_out, OP3);
  not not_115 (not_115_out, OP2);
  not not_116 (not_116_out, F14);
  not not_117 (not_117_out, F13);
  not not_118 (not_118_out, F12);
  not not_119 (not_119_out, OP4);
  not not_120 (not_120_out, OP3);
  not not_121 (not_121_out, F30);
  not not_122 (not_122_out, F25);
  not not_123 (not_123_out, F13);
  not not_124 (not_124_out, OP6);
  not not_125 (not_125_out, OP3);
  not not_126 (not_126_out, OP2);
  not not_127 (not_127_out, F30);
  not not_128 (not_128_out, F25);
  not not_129 (not_129_out, F14);
  not not_130 (not_130_out, F13);
  not not_131 (not_131_out, F12);
  not not_132 (not_132_out, OP6);
  not not_133 (not_133_out, OP3);
  not not_134 (not_134_out, OP2);
  not not_135 (not_135_out, F25);
  not not_136 (not_136_out, F14);
  not not_137 (not_137_out, F13);
  not not_138 (not_138_out, F12);
  not not_139 (not_139_out, OP6);
  not not_140 (not_140_out, OP3);
  not not_141 (not_141_out, OP2);
  not not_142 (not_142_out, F30);
  not not_143 (not_143_out, F25);
  not not_144 (not_144_out, OP6);
  not not_145 (not_145_out, OP3);
  not not_146 (not_146_out, OP2);
  not not_147 (not_147_out, F30);
  not not_148 (not_148_out, F25);
  not not_149 (not_149_out, F14);
  not not_150 (not_150_out, OP6);
  not not_151 (not_151_out, OP3);
  not not_152 (not_152_out, OP2);
  not not_153 (not_153_out, F14);
  not not_154 (not_154_out, F13);
  not not_155 (not_155_out, F12);
  not not_156 (not_156_out, OP6);
  not not_157 (not_157_out, OP5);
  not not_158 (not_158_out, OP3);
  not not_159 (not_159_out, OP2);
  not not_160 (not_160_out, OP6);
  not not_161 (not_161_out, OP5);
  not not_162 (not_162_out, OP3);
  not not_163 (not_163_out, OP2);
  not not_164 (not_164_out, F14);
  not not_165 (not_165_out, F12);
  not not_166 (not_166_out, OP6);
  not not_167 (not_167_out, OP5);
  not not_168 (not_168_out, OP4);
  not not_169 (not_169_out, OP3);
  not not_170 (not_170_out, OP2);
  not not_171 (not_171_out, F14);
  not not_172 (not_172_out, F12);
  not not_173 (not_173_out, OP6);
  not not_174 (not_174_out, OP4);
  not not_175 (not_175_out, OP3);
  not not_176 (not_176_out, OP2);
  not not_177 (not_177_out, F14);
  not not_178 (not_178_out, F13);
  not not_179 (not_179_out, F12);
  not not_180 (not_180_out, OP4);
  not not_181 (not_181_out, OP3);
  not not_182 (not_182_out, OP2);
  not not_183 (not_183_out, F14);
  not not_184 (not_184_out, F13);
  not not_185 (not_185_out, OP4);
  not not_186 (not_186_out, OP3);
  not not_187 (not_187_out, OP2);
  not not_188 (not_188_out, F14);
  not not_189 (not_189_out, F13);
  not not_190 (not_190_out, F12);
  not not_191 (not_191_out, OP4);
  not not_192 (not_192_out, OP3);
  not not_193 (not_193_out, F14);
  not not_194 (not_194_out, F13);
  not not_195 (not_195_out, OP6);
  not not_196 (not_196_out, OP4);
  not not_197 (not_197_out, OP3);
  not not_198 (not_198_out, OP2);
  not not_199 (not_199_out, F12);
  not not_200 (not_200_out, OP4);
  not not_201 (not_201_out, OP3);
  not not_202 (not_202_out, OP2);
  not not_203 (not_203_out, F30);
  not not_204 (not_204_out, F25);
  not not_205 (not_205_out, F12);
  not not_206 (not_206_out, OP6);
  not not_207 (not_207_out, OP3);
  not not_208 (not_208_out, OP2);
  not not_209 (not_209_out, F30);
  not not_210 (not_210_out, F25);
  not not_211 (not_211_out, F14);
  not not_212 (not_212_out, F12);
  not not_213 (not_213_out, OP6);
  not not_214 (not_214_out, OP3);
  not not_215 (not_215_out, OP2);
  not not_216 (not_216_out, F30);
  not not_217 (not_217_out, F25);
  not not_218 (not_218_out, F14);
  not not_219 (not_219_out, OP6);
  not not_220 (not_220_out, OP3);
  not not_221 (not_221_out, OP2);
  not not_222 (not_222_out, F12);
  not not_223 (not_223_out, OP6);
  not not_224 (not_224_out, OP5);
  not not_225 (not_225_out, OP3);
  not not_226 (not_226_out, OP2);
  not not_227 (not_227_out, F13);
  not not_228 (not_228_out, F12);
  not not_229 (not_229_out, OP6);
  not not_230 (not_230_out, OP5);
  not not_231 (not_231_out, OP3);
  not not_232 (not_232_out, OP2);
  not not_233 (not_233_out, F14);
  not not_234 (not_234_out, F12);
  not not_235 (not_235_out, OP6);
  not not_236 (not_236_out, OP5);
  not not_237 (not_237_out, OP3);
  not not_238 (not_238_out, OP2);
  not not_239 (not_239_out, F12);
  not not_240 (not_240_out, OP4);
  not not_241 (not_241_out, OP3);
  not not_242 (not_242_out, OP2);
  and and_1 (and_1_out, not_1_out, not_2_out, not_3_out, not_4_out, not_5_out, not_6_out, OP5, OP4, not_7_out, not_8_out);
  and and_2 (and_2_out, not_9_out, not_10_out, F14, F13, F12, not_11_out, OP5, OP4, not_12_out, not_13_out);
  and and_3 (and_3_out, not_14_out, not_15_out, not_16_out, F13, not_17_out, not_18_out, OP5, OP4, not_19_out, not_20_out);
  and and_4 (and_4_out, not_21_out, not_22_out, not_23_out, not_24_out, not_25_out, OP4, not_26_out, not_27_out);
  and and_5 (and_5_out, F14, F13, F12, not_28_out, not_29_out, OP4, not_30_out, not_31_out);
  and and_6 (and_6_out, F14, not_32_out, not_33_out, not_34_out, not_35_out, OP4, not_36_out, not_37_out);
  and and_7 (and_7_out, not_38_out, F13, not_39_out, not_40_out, not_41_out, OP4, not_42_out, not_43_out);
  and and_8 (and_8_out, F30, not_44_out, F14, not_45_out, F12, not_46_out, not_47_out, OP4, not_48_out, not_49_out);
  and and_9 (and_9_out, not_50_out, F13, not_51_out, not_52_out, not_53_out, not_54_out, not_55_out, not_56_out);
  and and_10 (and_10_out, not_57_out, F13, not_58_out, not_59_out, OP5, not_60_out, not_61_out, not_62_out);
  and and_11 (and_11_out, not_63_out, not_64_out, F12, not_65_out, OP5, not_66_out, not_67_out, not_68_out);
  and and_12 (and_12_out, F30, not_69_out, not_70_out, not_71_out, not_72_out, not_73_out, OP5, OP4, not_74_out, not_75_out);
  and and_13 (and_13_out, not_76_out, not_77_out, F14, F13, F12, not_78_out, OP5, OP4, not_79_out, not_80_out);
  and and_14 (and_14_out, not_81_out, not_82_out, not_83_out, F13, not_84_out, not_85_out, OP5, OP4, not_86_out, not_87_out);
  and and_15 (and_15_out, F14, F13, F12, not_88_out, not_89_out, OP4, not_90_out, not_91_out);
  and and_16 (and_16_out, not_92_out, F13, not_93_out, not_94_out, not_95_out, OP4, not_96_out, not_97_out);
  and and_17 (and_17_out, not_98_out, not_99_out, F14, not_100_out, F12, not_101_out, not_102_out, OP4, not_103_out, not_104_out);
  and and_18 (and_18_out, not_105_out, not_106_out, not_107_out, OP6, OP5, not_108_out, not_109_out, not_110_out);
  and and_19 (and_19_out, not_111_out, not_112_out, F12, OP6, OP5, not_113_out, not_114_out, not_115_out);
  and and_20 (and_20_out, not_116_out, not_117_out, not_118_out, OP6, OP5, not_119_out, not_120_out, OP2);
  and and_21 (and_21_out, not_121_out, not_122_out, F14, not_123_out, F12, not_124_out, OP5, OP4, not_125_out, not_126_out);
  and and_22 (and_22_out, not_127_out, not_128_out, not_129_out, not_130_out, not_131_out, not_132_out, OP5, OP4, not_133_out, not_134_out);
  and and_23 (and_23_out, F30, not_135_out, not_136_out, not_137_out, not_138_out, not_139_out, OP5, OP4, not_140_out, not_141_out);
  and and_24 (and_24_out, not_142_out, not_143_out, F14, F13, F12, not_144_out, OP5, OP4, not_145_out, not_146_out);
  and and_25 (and_25_out, not_147_out, not_148_out, not_149_out, F13, F12, not_150_out, OP5, OP4, not_151_out, not_152_out);
  and and_26 (and_26_out, not_153_out, not_154_out, not_155_out, not_156_out, not_157_out, OP4, not_158_out, not_159_out);
  and and_27 (and_27_out, F14, F13, F12, not_160_out, not_161_out, OP4, not_162_out, not_163_out);
  and and_28 (and_28_out, not_164_out, F13, not_165_out, not_166_out, not_167_out, not_168_out, not_169_out, not_170_out);
  and and_29 (and_29_out, not_171_out, F13, not_172_out, not_173_out, OP5, not_174_out, not_175_out, not_176_out);
  and and_30 (and_30_out, not_177_out, not_178_out, not_179_out, OP6, OP5, not_180_out, not_181_out, not_182_out);
  and and_31 (and_31_out, not_183_out, not_184_out, F12, OP6, OP5, not_185_out, not_186_out, not_187_out);
  and and_32 (and_32_out, not_188_out, not_189_out, not_190_out, OP6, OP5, not_191_out, not_192_out, OP2);
  and and_33 (and_33_out, not_193_out, not_194_out, F12, not_195_out, OP5, not_196_out, not_197_out, not_198_out);
  and and_34 (and_34_out, F14, F13, not_199_out, OP6, OP5, not_200_out, not_201_out, not_202_out);
  and and_35 (and_35_out, not_203_out, not_204_out, F14, F13, not_205_out, not_206_out, OP5, OP4, not_207_out, not_208_out);
  and and_36 (and_36_out, not_209_out, not_210_out, not_211_out, F13, not_212_out, not_213_out, OP5, OP4, not_214_out, not_215_out);
  and and_37 (and_37_out, not_216_out, not_217_out, not_218_out, F13, F12, not_219_out, OP5, OP4, not_220_out, not_221_out);
  and and_38 (and_38_out, F14, F13, not_222_out, not_223_out, not_224_out, OP4, not_225_out, not_226_out);
  and and_39 (and_39_out, F14, not_227_out, not_228_out, not_229_out, not_230_out, OP4, not_231_out, not_232_out);
  and and_40 (and_40_out, not_233_out, F13, not_234_out, not_235_out, not_236_out, OP4, not_237_out, not_238_out);
  and and_41 (and_41_out, F14, F13, not_239_out, OP6, OP5, not_240_out, not_241_out, not_242_out);
  or or_1 (S0, and_1_out, and_2_out, and_3_out, and_4_out, and_5_out, and_6_out, and_7_out, and_8_out, and_9_out, and_10_out, and_11_out);
  or or_2 (S1, and_12_out, and_13_out, and_14_out, and_15_out, and_16_out, and_17_out, and_18_out, and_19_out, and_20_out, and_21_out);
  or or_3 (S2, and_22_out, and_23_out, and_24_out, and_25_out, and_26_out, and_27_out, and_28_out, and_29_out, and_30_out, and_31_out, and_32_out, and_33_out, and_34_out);
  or or_4 (S3, and_35_out, and_36_out, and_37_out, and_38_out, and_39_out, and_40_out, and_41_out);
endmodule

// 控制信号生成
module \控制信号自动生成  (
  input  OP2,
  input  OP3,
  input  OP4,
  input  OP5,
  input  OP6,
  input  F12,
  input  F13,
  input  F14,
  input  F25,
  input  F30,
  output MemToReg,
  output U_Type,
  output MemWrite,
  output ALU_SRC,
  output RegWrite,
  output ecall,
  output S_Type,
  output BEQ,
  output BNE,
  output BLTU,
  output JALR,
  output JAL
);

  wire and_3_out, and_4_out, and_5_out, and_6_out, and_7_out, and_8_out, and_9_out, and_10_out, and_11_out,
       and_12_out, and_13_out, and_14_out, and_15_out, and_16_out, and_17_out, and_18_out, and_19_out,
       and_20_out, and_21_out, and_22_out, and_23_out, and_24_out, and_25_out, and_26_out, and_27_out,
       and_28_out, and_29_out, and_30_out, and_31_out, and_32_out, and_33_out, and_34_out, and_35_out,
       and_36_out, not_1_out, not_2_out, not_3_out, not_4_out, not_5_out, not_6_out, not_7_out, not_8_out,
       not_9_out, not_10_out, not_11_out, not_12_out, not_13_out, not_14_out, not_15_out, not_16_out,
       not_17_out, not_18_out, not_19_out, not_20_out, not_21_out, not_22_out, not_23_out, not_24_out,
       not_25_out, not_26_out, not_27_out, not_28_out, not_29_out, not_30_out, not_31_out, not_32_out,
       not_33_out, not_34_out, not_35_out, not_36_out, not_37_out, not_38_out, not_39_out, not_40_out,
       not_41_out, not_42_out, not_43_out, not_44_out, not_45_out, not_46_out, not_47_out, not_48_out,
       not_49_out, not_50_out, not_51_out, not_52_out, not_53_out, not_54_out, not_55_out, not_56_out,
       not_57_out, not_58_out, not_59_out, not_60_out, not_61_out, not_62_out, not_63_out, not_64_out,
       not_65_out, not_66_out, not_67_out, not_68_out, not_69_out, not_70_out, not_71_out, not_72_out,
       not_73_out, not_74_out, not_75_out, not_76_out, not_77_out, not_78_out, not_79_out, not_80_out,
       not_81_out, not_82_out, not_83_out, not_84_out, not_85_out, not_86_out, not_87_out, not_88_out,
       not_89_out, not_90_out, not_91_out, not_92_out, not_93_out, not_94_out, not_95_out, not_96_out,
       not_97_out, not_98_out, not_99_out, not_100_out, not_101_out, not_102_out, not_103_out, not_104_out,
       not_105_out, not_106_out, not_107_out, not_108_out, not_109_out, not_110_out, not_111_out,
       not_112_out, not_113_out, not_114_out, not_115_out, not_116_out, not_117_out, not_118_out,
       not_119_out, not_120_out, not_121_out, not_122_out, not_123_out, not_124_out, not_125_out,
       not_126_out, not_127_out, not_128_out, not_129_out, not_130_out, not_131_out, not_132_out,
       not_133_out, not_134_out, not_135_out, not_136_out, not_137_out, not_138_out, not_139_out,
       not_140_out, not_141_out, not_142_out, not_143_out, not_144_out, not_145_out, not_146_out,
       not_147_out, not_148_out, not_149_out, not_150_out, not_151_out, not_152_out, not_153_out,
       not_154_out, not_155_out, not_156_out, not_157_out, not_158_out, not_159_out, not_160_out,
       not_161_out, not_162_out, not_163_out, not_164_out, not_165_out, not_166_out, not_167_out,
       not_168_out, not_169_out, not_170_out, not_171_out, not_172_out, not_173_out, not_174_out,
       not_175_out, not_176_out, not_177_out, not_178_out, not_179_out, not_180_out, not_181_out,
       not_182_out, not_183_out, not_184_out, not_185_out, not_186_out, not_187_out, not_188_out,
       not_189_out, not_190_out, not_191_out, not_192_out, not_193_out, not_194_out, not_195_out,
       not_196_out, not_197_out, not_198_out, not_199_out, not_200_out, not_201_out, not_202_out,
       not_203_out, not_204_out, not_205_out, not_206_out, not_207_out, not_208_out, not_209_out,
       not_210_out, not_211_out, not_212_out, not_213_out, not_214_out, not_215_out, not_216_out,
       not_217_out, not_218_out, not_219_out, not_220_out, not_221_out, not_222_out, not_223_out,
       not_224_out, not_225_out, not_226_out, not_227_out, not_228_out, not_229_out, not_230_out,
       not_231_out, not_232_out, not_233_out, not_234_out, not_235_out, not_236_out, not_237_out,
       not_238_out, not_239_out;

  not not_1 (not_1_out, F14);
  not not_2 (not_2_out, F12);
  not not_3 (not_3_out, OP6);
  not not_4 (not_4_out, OP5);
  not not_5 (not_5_out, OP4);
  not not_6 (not_6_out, OP3);
  not not_7 (not_7_out, OP2);
  not not_8 (not_8_out, OP6);
  not not_9 (not_9_out, OP3);
  not not_10 (not_10_out, F14);
  not not_11 (not_11_out, F12);
  not not_12 (not_12_out, OP6);
  not not_13 (not_13_out, OP4);
  not not_14 (not_14_out, OP3);
  not not_15 (not_15_out, OP2);
  not not_16 (not_16_out, F14);
  not not_17 (not_17_out, F13);
  not not_18 (not_18_out, OP6);
  not not_19 (not_19_out, OP4);
  not not_20 (not_20_out, OP3);
  not not_21 (not_21_out, OP2);
  not not_22 (not_22_out, F14);
  not not_23 (not_23_out, F13);
  not not_24 (not_24_out, F12);
  not not_25 (not_25_out, OP6);
  not not_26 (not_26_out, OP5);
  not not_27 (not_27_out, OP3);
  not not_28 (not_28_out, OP2);
  not not_29 (not_29_out, OP6);
  not not_30 (not_30_out, OP5);
  not not_31 (not_31_out, OP3);
  not not_32 (not_32_out, OP2);
  not not_33 (not_33_out, F12);
  not not_34 (not_34_out, OP6);
  not not_35 (not_35_out, OP5);
  not not_36 (not_36_out, OP3);
  not not_37 (not_37_out, OP2);
  not not_38 (not_38_out, F13);
  not not_39 (not_39_out, F12);
  not not_40 (not_40_out, OP6);
  not not_41 (not_41_out, OP5);
  not not_42 (not_42_out, OP3);
  not not_43 (not_43_out, OP2);
  not not_44 (not_44_out, F14);
  not not_45 (not_45_out, F12);
  not not_46 (not_46_out, OP6);
  not not_47 (not_47_out, OP5);
  not not_48 (not_48_out, OP3);
  not not_49 (not_49_out, OP2);
  not not_50 (not_50_out, F30);
  not not_51 (not_51_out, F25);
  not not_52 (not_52_out, F14);
  not not_53 (not_53_out, F13);
  not not_54 (not_54_out, OP6);
  not not_55 (not_55_out, OP5);
  not not_56 (not_56_out, OP3);
  not not_57 (not_57_out, OP2);
  not not_58 (not_58_out, F30);
  not not_59 (not_59_out, F25);
  not not_60 (not_60_out, F13);
  not not_61 (not_61_out, OP6);
  not not_62 (not_62_out, OP5);
  not not_63 (not_63_out, OP3);
  not not_64 (not_64_out, OP2);
  not not_65 (not_65_out, F25);
  not not_66 (not_66_out, F13);
  not not_67 (not_67_out, OP6);
  not not_68 (not_68_out, OP5);
  not not_69 (not_69_out, OP3);
  not not_70 (not_70_out, OP2);
  not not_71 (not_71_out, F14);
  not not_72 (not_72_out, F12);
  not not_73 (not_73_out, OP6);
  not not_74 (not_74_out, OP5);
  not not_75 (not_75_out, OP4);
  not not_76 (not_76_out, OP3);
  not not_77 (not_77_out, OP2);
  not not_78 (not_78_out, F14);
  not not_79 (not_79_out, F12);
  not not_80 (not_80_out, OP6);
  not not_81 (not_81_out, OP4);
  not not_82 (not_82_out, OP3);
  not not_83 (not_83_out, OP2);
  not not_84 (not_84_out, F14);
  not not_85 (not_85_out, F13);
  not not_86 (not_86_out, F12);
  not not_87 (not_87_out, OP4);
  not not_88 (not_88_out, OP3);
  not not_89 (not_89_out, OP6);
  not not_90 (not_90_out, OP3);
  not not_91 (not_91_out, F14);
  not not_92 (not_92_out, F13);
  not not_93 (not_93_out, OP6);
  not not_94 (not_94_out, OP4);
  not not_95 (not_95_out, OP3);
  not not_96 (not_96_out, OP2);
  not not_97 (not_97_out, F30);
  not not_98 (not_98_out, F25);
  not not_99 (not_99_out, F14);
  not not_100 (not_100_out, F13);
  not not_101 (not_101_out, F12);
  not not_102 (not_102_out, OP6);
  not not_103 (not_103_out, OP3);
  not not_104 (not_104_out, OP2);
  not not_105 (not_105_out, F25);
  not not_106 (not_106_out, F14);
  not not_107 (not_107_out, F13);
  not not_108 (not_108_out, F12);
  not not_109 (not_109_out, OP6);
  not not_110 (not_110_out, OP3);
  not not_111 (not_111_out, OP2);
  not not_112 (not_112_out, F30);
  not not_113 (not_113_out, F25);
  not not_114 (not_114_out, OP6);
  not not_115 (not_115_out, OP3);
  not not_116 (not_116_out, OP2);
  not not_117 (not_117_out, F30);
  not not_118 (not_118_out, F25);
  not not_119 (not_119_out, F12);
  not not_120 (not_120_out, OP6);
  not not_121 (not_121_out, OP3);
  not not_122 (not_122_out, OP2);
  not not_123 (not_123_out, F30);
  not not_124 (not_124_out, F25);
  not not_125 (not_125_out, F14);
  not not_126 (not_126_out, F12);
  not not_127 (not_127_out, OP6);
  not not_128 (not_128_out, OP3);
  not not_129 (not_129_out, OP2);
  not not_130 (not_130_out, F30);
  not not_131 (not_131_out, F25);
  not not_132 (not_132_out, F14);
  not not_133 (not_133_out, OP6);
  not not_134 (not_134_out, OP3);
  not not_135 (not_135_out, OP2);
  not not_136 (not_136_out, F14);
  not not_137 (not_137_out, F13);
  not not_138 (not_138_out, F12);
  not not_139 (not_139_out, OP6);
  not not_140 (not_140_out, OP5);
  not not_141 (not_141_out, OP3);
  not not_142 (not_142_out, OP2);
  not not_143 (not_143_out, OP6);
  not not_144 (not_144_out, OP5);
  not not_145 (not_145_out, OP3);
  not not_146 (not_146_out, OP2);
  not not_147 (not_147_out, F12);
  not not_148 (not_148_out, OP6);
  not not_149 (not_149_out, OP5);
  not not_150 (not_150_out, OP3);
  not not_151 (not_151_out, OP2);
  not not_152 (not_152_out, F13);
  not not_153 (not_153_out, F12);
  not not_154 (not_154_out, OP6);
  not not_155 (not_155_out, OP5);
  not not_156 (not_156_out, OP3);
  not not_157 (not_157_out, OP2);
  not not_158 (not_158_out, F14);
  not not_159 (not_159_out, F12);
  not not_160 (not_160_out, OP6);
  not not_161 (not_161_out, OP5);
  not not_162 (not_162_out, OP3);
  not not_163 (not_163_out, OP2);
  not not_164 (not_164_out, F30);
  not not_165 (not_165_out, F25);
  not not_166 (not_166_out, F14);
  not not_167 (not_167_out, F13);
  not not_168 (not_168_out, OP6);
  not not_169 (not_169_out, OP5);
  not not_170 (not_170_out, OP3);
  not not_171 (not_171_out, OP2);
  not not_172 (not_172_out, F30);
  not not_173 (not_173_out, F25);
  not not_174 (not_174_out, F13);
  not not_175 (not_175_out, OP6);
  not not_176 (not_176_out, OP5);
  not not_177 (not_177_out, OP3);
  not not_178 (not_178_out, OP2);
  not not_179 (not_179_out, F25);
  not not_180 (not_180_out, F13);
  not not_181 (not_181_out, OP6);
  not not_182 (not_182_out, OP5);
  not not_183 (not_183_out, OP3);
  not not_184 (not_184_out, OP2);
  not not_185 (not_185_out, F14);
  not not_186 (not_186_out, F12);
  not not_187 (not_187_out, OP6);
  not not_188 (not_188_out, OP5);
  not not_189 (not_189_out, OP4);
  not not_190 (not_190_out, OP3);
  not not_191 (not_191_out, OP2);
  not not_192 (not_192_out, OP4);
  not not_193 (not_193_out, F14);
  not not_194 (not_194_out, F13);
  not not_195 (not_195_out, F12);
  not not_196 (not_196_out, OP4);
  not not_197 (not_197_out, OP3);
  not not_198 (not_198_out, F30);
  not not_199 (not_199_out, F25);
  not not_200 (not_200_out, F13);
  not not_201 (not_201_out, OP6);
  not not_202 (not_202_out, OP3);
  not not_203 (not_203_out, OP2);
  not not_204 (not_204_out, OP6);
  not not_205 (not_205_out, OP3);
  not not_206 (not_206_out, F30);
  not not_207 (not_207_out, F25);
  not not_208 (not_208_out, F14);
  not not_209 (not_209_out, F13);
  not not_210 (not_210_out, F12);
  not not_211 (not_211_out, OP3);
  not not_212 (not_212_out, OP2);
  not not_213 (not_213_out, F14);
  not not_214 (not_214_out, F12);
  not not_215 (not_215_out, OP6);
  not not_216 (not_216_out, OP4);
  not not_217 (not_217_out, OP3);
  not not_218 (not_218_out, OP2);
  not not_219 (not_219_out, F14);
  not not_220 (not_220_out, F13);
  not not_221 (not_221_out, F12);
  not not_222 (not_222_out, OP4);
  not not_223 (not_223_out, OP3);
  not not_224 (not_224_out, OP2);
  not not_225 (not_225_out, F14);
  not not_226 (not_226_out, F13);
  not not_227 (not_227_out, OP4);
  not not_228 (not_228_out, OP3);
  not not_229 (not_229_out, OP2);
  not not_230 (not_230_out, F12);
  not not_231 (not_231_out, OP4);
  not not_232 (not_232_out, OP3);
  not not_233 (not_233_out, OP2);
  not not_234 (not_234_out, F14);
  not not_235 (not_235_out, F13);
  not not_236 (not_236_out, F12);
  not not_237 (not_237_out, OP4);
  not not_238 (not_238_out, OP3);
  not not_239 (not_239_out, OP4);
  and and_1 (MemToReg, not_1_out, F13, not_2_out, not_3_out, not_4_out, not_5_out, not_6_out, not_7_out);
  and and_2 (U_Type, not_8_out, OP5, OP4, not_9_out, OP2);
  and and_3 (and_3_out, not_10_out, F13, not_11_out, not_12_out, OP5, not_13_out, not_14_out, not_15_out);
  and and_4 (and_4_out, not_16_out, not_17_out, F12, not_18_out, OP5, not_19_out, not_20_out, not_21_out);
  and and_5 (and_5_out, not_22_out, not_23_out, not_24_out, not_25_out, not_26_out, OP4, not_27_out, not_28_out);
  and and_6 (and_6_out, F14, F13, F12, not_29_out, not_30_out, OP4, not_31_out, not_32_out);
  and and_7 (and_7_out, F14, F13, not_33_out, not_34_out, not_35_out, OP4, not_36_out, not_37_out);
  and and_8 (and_8_out, F14, not_38_out, not_39_out, not_40_out, not_41_out, OP4, not_42_out, not_43_out);
  and and_9 (and_9_out, not_44_out, F13, not_45_out, not_46_out, not_47_out, OP4, not_48_out, not_49_out);
  and and_10 (and_10_out, not_50_out, not_51_out, not_52_out, not_53_out, F12, not_54_out, not_55_out, OP4, not_56_out, not_57_out);
  and and_11 (and_11_out, not_58_out, not_59_out, F14, not_60_out, F12, not_61_out, not_62_out, OP4, not_63_out, not_64_out);
  and and_12 (and_12_out, F30, not_65_out, F14, not_66_out, F12, not_67_out, not_68_out, OP4, not_69_out, not_70_out);
  and and_13 (and_13_out, not_71_out, F13, not_72_out, not_73_out, not_74_out, not_75_out, not_76_out, not_77_out);
  and and_14 (and_14_out, not_78_out, F13, not_79_out, not_80_out, OP5, not_81_out, not_82_out, not_83_out);
  and and_15 (and_15_out, not_84_out, not_85_out, not_86_out, OP6, OP5, not_87_out, not_88_out, OP2);
  and and_16 (and_16_out, not_89_out, OP5, OP4, not_90_out, OP2);
  and and_17 (and_17_out, not_91_out, not_92_out, F12, not_93_out, OP5, not_94_out, not_95_out, not_96_out);
  and and_18 (and_18_out, not_97_out, not_98_out, not_99_out, not_100_out, not_101_out, not_102_out, OP5, OP4, not_103_out, not_104_out);
  and and_19 (and_19_out, F30, not_105_out, not_106_out, not_107_out, not_108_out, not_109_out, OP5, OP4, not_110_out, not_111_out);
  and and_20 (and_20_out, not_112_out, not_113_out, F14, F13, F12, not_114_out, OP5, OP4, not_115_out, not_116_out);
  and and_21 (and_21_out, not_117_out, not_118_out, F14, F13, not_119_out, not_120_out, OP5, OP4, not_121_out, not_122_out);
  and and_22 (and_22_out, not_123_out, not_124_out, not_125_out, F13, not_126_out, not_127_out, OP5, OP4, not_128_out, not_129_out);
  and and_23 (and_23_out, not_130_out, not_131_out, not_132_out, F13, F12, not_133_out, OP5, OP4, not_134_out, not_135_out);
  and and_24 (and_24_out, not_136_out, not_137_out, not_138_out, not_139_out, not_140_out, OP4, not_141_out, not_142_out);
  and and_25 (and_25_out, F14, F13, F12, not_143_out, not_144_out, OP4, not_145_out, not_146_out);
  and and_26 (and_26_out, F14, F13, not_147_out, not_148_out, not_149_out, OP4, not_150_out, not_151_out);
  and and_27 (and_27_out, F14, not_152_out, not_153_out, not_154_out, not_155_out, OP4, not_156_out, not_157_out);
  and and_28 (and_28_out, not_158_out, F13, not_159_out, not_160_out, not_161_out, OP4, not_162_out, not_163_out);
  and and_29 (and_29_out, not_164_out, not_165_out, not_166_out, not_167_out, F12, not_168_out, not_169_out, OP4, not_170_out, not_171_out);
  and and_30 (and_30_out, not_172_out, not_173_out, F14, not_174_out, F12, not_175_out, not_176_out, OP4, not_177_out, not_178_out);
  and and_31 (and_31_out, F30, not_179_out, F14, not_180_out, F12, not_181_out, not_182_out, OP4, not_183_out, not_184_out);
  and and_32 (and_32_out, not_185_out, F13, not_186_out, not_187_out, not_188_out, not_189_out, not_190_out, not_191_out);
  and and_33 (and_33_out, OP6, OP5, not_192_out, OP3, OP2);
  and and_34 (and_34_out, not_193_out, not_194_out, not_195_out, OP6, OP5, not_196_out, not_197_out, OP2);
  and and_35 (and_35_out, not_198_out, not_199_out, F14, not_200_out, F12, not_201_out, OP5, OP4, not_202_out, not_203_out);
  and and_36 (and_36_out, not_204_out, OP5, OP4, not_205_out, OP2);
  and and_37 (ecall, not_206_out, not_207_out, not_208_out, not_209_out, not_210_out, OP6, OP5, OP4, not_211_out, not_212_out);
  and and_38 (S_Type, not_213_out, F13, not_214_out, not_215_out, OP5, not_216_out, not_217_out, not_218_out);
  and and_39 (BEQ, not_219_out, not_220_out, not_221_out, OP6, OP5, not_222_out, not_223_out, not_224_out);
  and and_40 (BNE, not_225_out, not_226_out, F12, OP6, OP5, not_227_out, not_228_out, not_229_out);
  and and_41 (BLTU, F14, F13, not_230_out, OP6, OP5, not_231_out, not_232_out, not_233_out);
  and and_42 (JALR, not_234_out, not_235_out, not_236_out, OP6, OP5, not_237_out, not_238_out, OP2);
  and and_43 (JAL, OP6, OP5, not_239_out, OP3, OP2);
  or or_1 (MemWrite, and_3_out, and_4_out);
  or or_2 (ALU_SRC, and_5_out, and_6_out, and_7_out, and_8_out, and_9_out, and_10_out, and_11_out, and_12_out, and_13_out, and_14_out, and_15_out, and_16_out, and_17_out);
  or or_3 (RegWrite, and_18_out, and_19_out, and_20_out, and_21_out, and_22_out, and_23_out, and_24_out, and_25_out, and_26_out, and_27_out, and_28_out, and_29_out, and_30_out, and_31_out, and_32_out, and_33_out, and_34_out, and_35_out, and_36_out);
endmodule

// ALU
module ALU (
  input  [31:0] X,
  input  [31:0] Y,
  input  [3:0] AluOP,
  output out_4,
  output Equal,
  output out_6,
  output [31:0] Result,
  output [31:0] Result_2
);

  wire [0:0] comparator_1_lt, comparator_2_lt;
  wire [31:0] adder_1_out, AND_out, divider_1_out, divider_1_rem, multiplier_1_cout, multiplier_1_out,
       NOR_out, OR_out, shifter_1_out, shifter_2_out, shifter_3_out, subtractor_1_out, XOR_out;

  assign AND_out = X & Y;  // AND_Gate AND, 32 bits wide
  assign OR_out = X | Y;  // OR_Gate OR, 32 bits wide
  Shifter #(.width(32), .shift("ll")) shifter_1 (.in(X), .\dist (Y[4:0]), .out(shifter_1_out));
  Shifter #(.width(32), .shift("ar")) shifter_2 (.in(X), .\dist (Y[4:0]), .out(shifter_2_out));
  Shifter #(.width(32), .shift("lr")) shifter_3 (.in(X), .\dist (Y[4:0]), .out(shifter_3_out));
  Multiplier #(.width(32)) multiplier_1 (.a(X), .b(Y), .out(multiplier_1_out), .cout(multiplier_1_cout));  // open: cin
  Divider #(.width(32)) divider_1 (.a(X), .b(Y), .out(divider_1_out), .rem(divider_1_rem));  // open: upper
  Adder #(.width(32)) adder_1 (.a(X), .b(Y), .out(adder_1_out));  // open: cin, cout
  Subtractor #(.width(32)) subtractor_1 (.a(X), .b(Y), .out(subtractor_1_out));  // open: bin, bout
  assign XOR_out = X ^ Y;  // XOR_Gate XOR, 32 bits wide
  assign NOR_out = ~(X | Y);  // NOR_Gate NOR, 32 bits wide
  Comparator #(.width(32), .mode("twosComplement")) comparator_1 (
    .a(X), .b(Y), .eq(Equal), .lt(comparator_1_lt[0]));  // open: gt
  Comparator #(.width(32), .mode("unsigned")) comparator_2 (.a(X), .b(Y), .lt(comparator_2_lt[0]));  // open: gt, eq
  Multiplexer #(.select(4), .width(32), .disabled("Z"), .enable("false")) multiplexer_1 (
    .in0(shifter_1_out), .in1(shifter_2_out), .in2(shifter_3_out), .in3(multiplier_1_out),
    .in4(divider_1_out), .in5(adder_1_out), .in6(subtractor_1_out), .in7(AND_out), .in8(OR_out),
    .in9(XOR_out), .in10(NOR_out), .in11({{31{1'b0}}, comparator_1_lt[0]}),
    .in12({{31{1'b0}}, comparator_2_lt[0]}), .in13({32{1'b0}}), .in14({32{1'b0}}), .in15({32{1'b0}}),
    .out(Result), .sel(AluOP));
  Multiplexer #(.select(4), .width(32), .disabled("Z"), .enable("false")) multiplexer_2 (
    .in0({32{1'b0}}), .in1({32{1'b0}}), .in2({32{1'b0}}), .in3(multiplier_1_cout), .in4(divider_1_rem),
    .in5({32{1'b0}}), .in6({32{1'b0}}), .in7({32{1'b0}}), .in8({32{1'b0}}), .in9({32{1'b0}}),
    .in10({32{1'b0}}), .in11({32{1'b0}}), .in12({32{1'b0}}), .in13({32{1'b0}}), .in14({32{1'b0}}),
    .in15({32{1'b0}}), .out(Result_2), .sel(AluOP));
  Multiplexer #(.select(4), .width(1), .disabled("Z"), .enable("false")) multiplexer_3 (
    .in0(1'b0), .in1(1'b0), .in2(1'b0), .in3(1'b0), .in4(1'b0), .in5(1'b0), .in6(1'b0), .in7(1'b0),
    .in8(1'b0), .in9(1'b0), .in10(1'b0), .in11(comparator_1_lt[0]), .in12(comparator_2_lt[0]), .in13(1'b0),
    .in14(1'b0), .in15(1'b0), .out(out_6), .sel(AluOP));
  not not_1 (out_4, out_6);

  // Other names for the same wires on the sheet: Result2[31:0] = Result_2; S[3:0] = AluOP; tunnel = out_6;
  //   tunnel_t = out_4

  // Notes on the sheet:
  //   不要改变此引脚区域内容，也不要改变ALU封装形式
  //   输入引脚
  //   输出引脚
endmodule

module Regifile (
  input  [31:0] Din,
  input  Clk,
  input  WE,
  input  [4:0] R1_num,
  input  [4:0] W_num,
  input  [4:0] R2_num,
  output [31:0] R1,
  output [31:0] R2
);

  // RegisterFile registerfile_1: pin names not known; wires that end beside it: Din, Clk, WE, W_num, R1_num, R2_num, R1, R2
endmodule

module Regifile_FailingEdge (
  input  [31:0] Din,
  input  Clk,
  input  WE,
  input  [4:0] R1_num,
  input  [4:0] W_num,
  input  [4:0] R2_num,
  output [31:0] R1,
  output [31:0] R2
);

  // RegisterFile registerfile_1: pin names not known; wires that end beside it: Din, Clk, WE, W_num, R1_num, R2_num, R1, R2
endmodule

module \理想流水线  (
  output RegWrite,
  output MemWrite,
  output [31:0] IF_PC,
  output [31:0] ID_PC,
  output [31:0] EX_PC,
  output [31:0] M_PC,
  output [31:0] WB_PC,
  output [31:0] RDin,
  output [31:0] MDin,
  output [31:0] LedData
);

  wire alu_1_equal, alu_1_out_6, and_1_out, and_2_out, and_3_out, and_4_out, and_5_out, CLK, clock_1_out,
       comparator_1_eq, comparator_1_lt, comparator_2_eq, d_ff_1_q, Go, halt, IR1, IR2, IR3, nand_1_out,
       not_1_out, not_2_out, not_3_out, not_4_out, or_1_out, riscv_probe_4_p9, RST, undriven, undriven_2,
       undriven_3, undriven_4, undriven_5, undriven_7, undriven_8, undriven_15, undriven_16, undriven_18, W1,
       W2, W3, \单周期硬布线控制器_1_alu_src , \单周期硬布线控制器_1_beq , \单周期硬布线控制器_1_bltu , \单周期硬布线控制器_1_bne ,
       \单周期硬布线控制器_1_ecall , \单周期硬布线控制器_1_jal , \单周期硬布线控制器_1_jalr , \单周期硬布线控制器_1_memtoreg ,
       \单周期硬布线控制器_1_memwrite , \单周期硬布线控制器_1_regwrite , \单周期硬布线控制器_1_uret ;
  wire [1:0] priority_encoder_1_out, undriven_22, \单周期硬布线控制器_1_s_type ;
  wire [3:0] undriven_6, \单周期硬布线控制器_1_alu_op ;
  wire [4:0] multiplexer_2_out, multiplexer_3_out, undriven_19;
  wire [12:0] CNT_num;
  wire [15:0] \LoadUse次数 , \总周期数 , \插入气泡数 , \无条件分支数 , \条件分支成功数 ;
  wire [31:0] adder_2_out, adder_3_out, alu_1_result, bit_extender_1_out, bit_extender_2_out,
       bit_extender_3_out, bit_extender_4_out, EX_IR, ID_IR, IF_IR, MEM_IR, multiplexer_1_out,
       multiplexer_4_out, multiplexer_5_out, ram_1_data, regifile_1_r1, regifile_1_r2, riscv_probe_4_p4,
       shifter_1_out, shifter_2_out, undriven_9, undriven_10, undriven_11, undriven_12, undriven_13,
       undriven_14, undriven_17, undriven_20, undriven_21, WB_IR;

  Button \u_总复位  (.out(RST));
  Button _1 (.out(IR1));
  Button _2 (.out(IR2));
  Button _3 (.out(IR3));
  // Probe on \总周期数 
  // Probe on \总周期数 
  Button \u_继续运行  (.out(Go));
  LED #(.active("true")) led_1 (.in(W1));
  LED #(.active("true")) led_2 (.in(W2));
  LED #(.active("true")) led_3 (.in(W3));
  Hex_Digit_Display hex_digit_display_1 (.value(LedData[31:28]));  // open: dp
  // Probe on IF_PC[19:0]
  // RiscV_Probe riscv_probe_1: pin names not known; wires that end beside it: IF_IR
  Multiplexer #(.select(2), .width(32), .disabled("Z"), .enable("false")) multiplexer_1 (
    .in0(riscv_probe_4_p4), .in1(alu_1_result), .in2(adder_2_out), .in3(adder_3_out),
    .out(multiplexer_1_out), .sel(priority_encoder_1_out));
  Hex_Digit_Display hex_digit_display_2 (.value(LedData[23:20]));  // open: dp
  Hex_Digit_Display hex_digit_display_3 (.value(LedData[27:24]));  // open: dp
  // Probe on ID_PC[19:0]
  // RiscV_Probe riscv_probe_2: pin names not known; wires that end beside it: ID_IR
  Register #(.width(32), .trigger("rising"), .Select("low")) PC (
    .D(multiplexer_1_out), .en(not_1_out), .Q(IF_PC), .clk(CLK), .clr(RST));
  not not_1 (not_1_out, halt);
  Hex_Digit_Display hex_digit_display_4 (.value(LedData[19:16]));  // open: dp
  Hex_Digit_Display hex_digit_display_5 (.value(LedData[15:12]));  // open: dp
  Hex_Digit_Display hex_digit_display_6 (.value(LedData[7:4]));  // open: dp
  Hex_Digit_Display hex_digit_display_7 (.value(LedData[11:8]));  // open: dp
  // Probe on EX_PC[19:0]
  // RiscV_Probe riscv_probe_3: pin names not known; wires that end beside it: EX_IR
  // RiscV_Probe riscv_probe_4: pin names not known; wires that end beside it: IF_IR, IF_IR, IF_PC, riscv_probe_4_p4, 1'b0, CLK, ID_IR, ID_PC, riscv_probe_4_p9, RST, ID_IR[31:20], {ID_IR[31:25], ID_IR[11:7]}, ID_IR[31:12]
  Hex_Digit_Display hex_digit_display_8 (.value(LedData[3:0]));  // open: dp
  ROM #(.addrWidth(10), .dataWidth(32), .Select("high")) rom_1 (.addr(IF_PC[11:2]), .data(IF_IR));
  Adder #(.width(32)) adder_1 (.a(IF_PC), .b(32'h4), .out(riscv_probe_4_p4));  // open: cin, cout
  // Probe on \总周期数 
  // Probe on M_PC[19:0]
  // RiscV_Probe riscv_probe_5: pin names not known; wires that end beside it: MEM_IR, 1'b0
  // Probe on \总周期数 
  // Probe on \无条件分支数 
  // Probe on \条件分支成功数 
  // Probe on \插入气泡数 
  // Probe on \LoadUse次数 
  // Probe on IF_PC[11:0]
  // Probe on WB_PC[19:0]
  // RiscV_Probe riscv_probe_6: pin names not known; wires that end beside it: WB_IR
  \单周期硬布线控制器  \u_单周期硬布线控制器_1  (
    .Funct({ID_IR[30], ID_IR[25], ID_IR[14:12]}), .OP(ID_IR[6:2]), .ALU_OP(\单周期硬布线控制器_1_alu_op ),
    .MemToReg(\单周期硬布线控制器_1_memtoreg ), .MemWrite(\单周期硬布线控制器_1_memwrite ), .ALU_SRC(\单周期硬布线控制器_1_alu_src ),
    .RegWrite(\单周期硬布线控制器_1_regwrite ), .ecall(\单周期硬布线控制器_1_ecall ), .S_type(\单周期硬布线控制器_1_s_type [0]),
    .Jalr(\单周期硬布线控制器_1_jalr ), .Beq(\单周期硬布线控制器_1_beq ), .JAL(\单周期硬布线控制器_1_jal ), .Bne(\单周期硬布线控制器_1_bne ),
    .in_3(ID_IR[21]), .uret(\单周期硬布线控制器_1_uret ), .U_Type(\单周期硬布线控制器_1_s_type [1]), .BLTU(\单周期硬布线控制器_1_bltu ));
  Multiplexer #(.select(1), .width(5), .disabled("Z"), .enable("false")) multiplexer_2 (
    .in0(ID_IR[19:15]), .in1(5'b10001), .out(multiplexer_2_out), .sel(\单周期硬布线控制器_1_ecall ));
  Multiplexer #(.select(1), .width(5), .disabled("Z"), .enable("false")) multiplexer_3 (
    .in0(ID_IR[24:20]), .in1(5'b01010), .out(multiplexer_3_out), .sel(\单周期硬布线控制器_1_ecall ));
  assign bit_extender_1_out = {{20{ID_IR[31]}}, ID_IR[31:20]};  // Bit_Extender bit_extender_1
  assign bit_extender_2_out = {{20{ID_IR[31]}}, {ID_IR[31:25], ID_IR[11:7]}};  // Bit_Extender bit_extender_2
  // Probe on ID_PC[11:0]
  // Probe on EX_PC[11:0]
  Multiplexer #(.select(2), .width(32), .disabled("Z"), .enable("false")) multiplexer_4 (
    .in0(bit_extender_1_out), .in1(bit_extender_2_out), .in2({ID_IR[31:12], {12{1'b0}}}),
    .out(multiplexer_4_out), .sel(\单周期硬布线控制器_1_s_type ));  // open: in3
  // Probe on M_PC[11:0]
  D_Flip_Flop #(.trigger("high"), .Pre_Clr_Positions("LEGACY"), .NegatePresetClear("false"), .enable("true"), .NewFFLayout("false")) d_ff_1 (.Q(d_ff_1_q));  // open: clk, D, Qn, preset, en, reset
  // Probe on 13'hc
  assign bit_extender_3_out = {{20{ID_IR[31]}}, {ID_IR[31], ID_IR[7], ID_IR[30:25], ID_IR[11:8]}};  // Bit_Extender bit_extender_3
  assign bit_extender_4_out = {{12{ID_IR[31]}}, {ID_IR[31], ID_IR[19:12], ID_IR[20], ID_IR[30:21]}};  // Bit_Extender bit_extender_4
  // Probe on WB_PC[11:0]
  Comparator #(.width(13), .mode("twosComplement")) comparator_1 (
    .a(CNT_num), .b(13'hc), .eq(comparator_1_eq), .lt(comparator_1_lt));  // open: gt
  Clock #(.highDuration(1), .lowDuration(1)) clock_1 (.out(clock_1_out));
  Regifile regifile_1 (
    .Din(RDin), .Clk(CLK), .R1(regifile_1_r1), .R2(regifile_1_r2), .WE(RegWrite), .W_num(undriven_19),
    .R1_num(multiplexer_2_out), .R2_num(multiplexer_3_out));
  Shifter #(.width(32), .shift("ll")) shifter_1 (.in(bit_extender_3_out), .\dist (5'b00001), .out(shifter_1_out));
  Shifter #(.width(32), .shift("ll")) shifter_2 (.in(bit_extender_4_out), .\dist (5'b00001), .out(shifter_2_out));
  nand nand_1 (nand_1_out, d_ff_1_q, comparator_1_eq);
  Counter #(.width(13), .max('h1fff), .ongoal("stay"), .trigger("rising"), .behavior("old")) counter_1 (
    .count(comparator_1_lt), .Q(CNT_num), .clk(clock_1_out));  // open: load, D, carry, clr, preset
  assign CLK = nand_1_out ? clock_1_out : 1'bz;  // Controlled_Buffer controlled_buffer_1
  Pull_Resistor #(.pull(1)) pull_resistor_1 (.node(CLK));
  or or_1 (or_1_out, and_5_out, and_3_out, and_4_out);
  Priority_Encoder #(.select(2), .disabled("Z")) priority_encoder_1 (
    .in0(1'b1), .in1(undriven), .in2(or_1_out), .in3(undriven_2), .out(priority_encoder_1_out));  // open: gs, en_out, en_in
  Comparator #(.width(32), .mode("twosComplement")) comparator_2 (
    .a(undriven_9), .b(32'h22), .eq(comparator_2_eq));  // open: gt, lt
  and and_1 (and_1_out, comparator_2_eq, undriven_8);
  not not_2 (not_2_out, comparator_2_eq);
  and and_2 (and_2_out, not_2_out, undriven_8);
  not not_3 (not_3_out, halt);
  and and_3 (and_3_out, undriven_4, not_4_out);
  and and_4 (and_4_out, undriven_3, alu_1_equal);
  Multiplexer #(.select(1), .width(32), .disabled("Z"), .enable("false")) multiplexer_5 (
    .in0(undriven_13), .in1(undriven_10), .out(multiplexer_5_out), .sel(undriven_7));
  Register #(.width(32), .trigger("rising"), .Select("low")) register_1 (
    .D(undriven_13), .en(and_1_out), .Q(LedData), .clk(CLK));  // open: clr
  Counter #(.width(16), .max('hffff), .ongoal("wrap"), .trigger("rising"), .behavior("new")) counter_2 (
    .count(not_3_out), .Q(\总周期数 ), .clk(CLK));  // open: load, D, carry, clr, preset, down
  and and_5 (and_5_out, undriven_5, alu_1_out_6);
  not not_4 (not_4_out, alu_1_equal);
  ALU alu_1 (
    .X(undriven_9), .Y(multiplexer_5_out), .AluOP(undriven_6), .Equal(alu_1_equal), .Result(alu_1_result),
    .out_6(alu_1_out_6));  // open: Result_2, out_4
  Adder #(.width(32)) adder_2 (.a(EX_PC), .b(undriven_11), .out(adder_2_out));  // open: cin, cout
  Adder #(.width(32)) adder_3 (.a(EX_PC), .b(undriven_12), .out(adder_3_out));  // open: cin, cout
  RAM #(.addrWidth(10), .dataWidth(32), .bus("separate"), .Select("high")) ram_1 (
    .addr(MDin[11:2]), .din(undriven_14), .data(ram_1_data), .str(MemWrite), .sel(1'b1), .clk(CLK),
    .ld(1'b1), .clr(RST));
  or or_2 (undriven_22[1], undriven_16, undriven_15);
  Multiplexer #(.select(2), .width(32), .disabled("Z"), .enable("false")) multiplexer_6 (
    .in0(undriven_17), .in1(undriven_20), .in2(undriven_21), .out(RDin), .sel(undriven_22));  // open: in3
  Multiplexer #(.select(1), .width(1), .disabled("Z"), .enable("false")) multiplexer_7 (
    .in0(undriven_18), .in1(1'b0), .out(halt), .sel(Go));

  // Other names for the same wires on the sheet: MEM_PC[31:0] = M_PC

  // Notes on the sheet:
  //   中断源
  //   时空图监测，可删除
  //   中断等待指示
  //   BranchTaken
  //   BranchAddr
  //   数码管输出
  //   取指
  //   指令存储器
  //   指令探针
  //   contents of rom_1 (hex, n*v repeats v):
  //   413 493 913 993 46413 14e493 296913 39e993 842023 942223 1242423 1342623 a00893 493 913 993 73
  //   JAL
  //   rs1
  //   rs2
  //   I
  //   S
  //   *U:imm[31:12]
  //   Beq
  //   Bne
  //   JALR
  //   URET
  //   rd
  //   B:imm[12:0]
  //   J:imm[20:0]
  //   控制位
  //   译码
  //   BLTU
  //   MemToReg
  //   MemWrite
  //   AluOP
  //   AluSrcB
  //   RegWrite
  //   U_type
  //   S_type
  //   WriteReg#
  //   流水调试日志用
  //   暂停节拍，不能为0
  //   WriteBackData
  //   戳工具置1进入计数暂停模式，ctrl+k时钟自动运行到对应节拍暂停
  //   ctrl+k关闭时钟连续运行，将控制位置零，进入单步调试模式调试
  //   用这个时钟源需要去掉电路中的其他时钟源
  //   可计数暂停的时钟源
  //   BranchTaken
  //   执行
  //   BranchAddr
  //   为方便自动评测，需要输出流水线各段保存的PC值，注意是PC不是PC+4，另外ID段寄存器写入信息，Mem段内存写入信息也要输出
  //   ALU_result
  //   访存
  //   数据存储器
  //   ALU_result
  //   Data
  //   MemToReg
  //   WriteBackData
  //   写回
  //   JAL or JALR
  //   WriteReg#
endmodule

module \气泡流水线  (
  output RegWrite,
  output MemWrite,
  output [31:0] IF_PC,
  output [31:0] ID_PC,
  output [31:0] EX_PC,
  output [31:0] M_PC,
  output [31:0] WB_PC,
  output [31:0] RDin,
  output [31:0] MDin,
  output [31:0] LedData
);

  wire alu_1_equal, alu_1_out_6, and_1_out, and_2_out, and_3_out, and_4_out, and_5_out, CLK, clock_1_out,
       comparator_1_eq, comparator_1_lt, comparator_2_eq, d_ff_1_q, DataCorrelate, Go, halt, IR1, IR2, IR3,
       nand_1_out, not_1_out, not_2_out, not_3_out, not_4_out, or_1_out, or_3_out, or_4_out, or_5_out,
       riscv_probe_4_p5, riscv_probe_4_p9, RST, undriven_2, undriven_4, undriven_5, undriven_6, undriven_13,
       undriven_14, undriven_15, undriven_16, undriven_17, undriven_20, undriven_21, undriven_22, W1, W2, W3,
       \单周期硬布线控制器_1_alu_src , \单周期硬布线控制器_1_beq , \单周期硬布线控制器_1_bltu , \单周期硬布线控制器_1_bne , \单周期硬布线控制器_1_ecall ,
       \单周期硬布线控制器_1_jal , \单周期硬布线控制器_1_jalr , \单周期硬布线控制器_1_memtoreg , \单周期硬布线控制器_1_memwrite ,
       \单周期硬布线控制器_1_regwrite , \单周期硬布线控制器_1_uret , \源寄存器使用情况_1_rs1_used , \源寄存器使用情况_1_rs2_used ;
  wire [1:0] priority_encoder_1_out, undriven_26, \单周期硬布线控制器_1_s_type ;
  wire [3:0] undriven_3, \单周期硬布线控制器_1_alu_op ;
  wire [4:0] multiplexer_2_out, multiplexer_3_out, undriven, undriven_10, undriven_18;
  wire [11:2] undriven_19;
  wire [12:0] CNT_num;
  wire [15:0] \LoadUse次数 , \总周期数 , \插入气泡数 , \无条件分支数 , \条件分支成功数 ;
  wire [31:0] adder_2_out, adder_3_out, alu_1_result, bit_extender_1_out, bit_extender_2_out,
       bit_extender_3_out, bit_extender_4_out, EX_IR, ID_IR, IF_IR, MEM_IR, multiplexer_1_out,
       multiplexer_4_out, multiplexer_5_out, ram_1_data, regifile_failingedge_1_r1,
       regifile_failingedge_1_r2, riscv_probe_4_p4, shifter_1_out, shifter_2_out, undriven_7, undriven_8,
       undriven_9, undriven_11, undriven_12, undriven_23, undriven_24, undriven_25, WB_IR;

  Button \u_总复位  (.out(RST));
  Button _1 (.out(IR1));
  Button _2 (.out(IR2));
  Button _3 (.out(IR3));
  // Probe on \总周期数 
  // Probe on \总周期数 
  Button \u_继续运行  (.out(Go));
  LED #(.active("true")) led_1 (.in(W1));
  LED #(.active("true")) led_2 (.in(W2));
  LED #(.active("true")) led_3 (.in(W3));
  Hex_Digit_Display hex_digit_display_1 (.value(LedData[31:28]));  // open: dp
  // Probe on IF_PC[19:0]
  // RiscV_Probe riscv_probe_1: pin names not known; wires that end beside it: IF_IR
  Hex_Digit_Display hex_digit_display_2 (.value(LedData[23:20]));  // open: dp
  Hex_Digit_Display hex_digit_display_3 (.value(LedData[27:24]));  // open: dp
  // Probe on ID_PC[19:0]
  // RiscV_Probe riscv_probe_2: pin names not known; wires that end beside it: ID_IR
  Multiplexer #(.select(2), .width(32), .disabled("Z"), .enable("false")) multiplexer_1 (
    .in0(riscv_probe_4_p4), .in1(alu_1_result), .in2(adder_2_out), .in3(adder_3_out),
    .out(multiplexer_1_out), .sel(priority_encoder_1_out));
  not not_1 (not_1_out, or_1_out);
  or or_1 (or_1_out, DataCorrelate, halt);
  Hex_Digit_Display hex_digit_display_4 (.value(LedData[19:16]));  // open: dp
  Hex_Digit_Display hex_digit_display_5 (.value(LedData[15:12]));  // open: dp
  Register #(.width(32), .trigger("rising"), .Select("low")) PC (
    .D(multiplexer_1_out), .en(not_1_out), .Q(IF_PC), .clk(CLK), .clr(RST));
  Hex_Digit_Display hex_digit_display_6 (.value(LedData[11:8]));  // open: dp
  Hex_Digit_Display hex_digit_display_7 (.value(LedData[7:4]));  // open: dp
  // Probe on EX_PC[19:0]
  // RiscV_Probe riscv_probe_3: pin names not known; wires that end beside it: EX_IR
  Hex_Digit_Display hex_digit_display_8 (.value(LedData[3:0]));  // open: dp
  ROM #(.addrWidth(10), .dataWidth(32), .Select("high")) rom_1 (.addr(IF_PC[11:2]), .data(IF_IR));
  // RiscV_Probe riscv_probe_4: pin names not known; wires that end beside it: IF_IR, IF_IR, IF_PC, riscv_probe_4_p4, riscv_probe_4_p5, CLK, ID_IR, ID_PC, riscv_probe_4_p9, RST, ID_IR[31:20], {ID_IR[31:25], ID_IR[11:7]}, ID_IR[31:12]
  Adder #(.width(32)) adder_1 (.a(IF_PC), .b(32'h4), .out(riscv_probe_4_p4));  // open: cin, cout
  // Probe on \总周期数 
  // Probe on M_PC[19:0]
  // RiscV_Probe riscv_probe_5: pin names not known; wires that end beside it: MEM_IR
  or or_2 (riscv_probe_4_p5, DataCorrelate, halt);
  // Probe on \总周期数 
  // Probe on \无条件分支数 
  // Probe on \条件分支成功数 
  // Probe on \插入气泡数 
  // Probe on \LoadUse次数 
  \源寄存器使用情况  \u_源寄存器使用情况_1  (
    .OP(ID_IR[6:2]), .Funct({ID_IR[30], ID_IR[25], ID_IR[14:12]}), .rs1_used(\源寄存器使用情况_1_rs1_used ),
    .rs2_used(\源寄存器使用情况_1_rs2_used ));
  // Probe on IF_PC[11:0]
  // Probe on WB_PC[19:0]
  // RiscV_Probe riscv_probe_6: pin names not known; wires that end beside it: WB_IR
  \数据相关检测  \u_数据相关检测  (
    .rs1(multiplexer_2_out), .rs2(multiplexer_3_out), .rs1_used(\源寄存器使用情况_1_rs1_used ),
    .EX_RegWrite(undriven_5), .EX_rd(undriven_10), .rs2_used(\源寄存器使用情况_1_rs2_used ),
    .MEM_RegWrite(undriven_17), .MEM_rd(undriven_18), .DataCorrelate(DataCorrelate));  // open: rs1Fwd, rs2Fwd, EX_MemToReg, LoadUse
  Multiplexer #(.select(1), .width(5), .disabled("Z"), .enable("false")) multiplexer_2 (
    .in0(ID_IR[19:15]), .in1(5'b10001), .out(multiplexer_2_out), .sel(\单周期硬布线控制器_1_ecall ));
  Multiplexer #(.select(1), .width(5), .disabled("Z"), .enable("false")) multiplexer_3 (
    .in0(ID_IR[24:20]), .in1(5'b01010), .out(multiplexer_3_out), .sel(\单周期硬布线控制器_1_ecall ));
  assign bit_extender_1_out = {{20{ID_IR[31]}}, ID_IR[31:20]};  // Bit_Extender bit_extender_1
  assign bit_extender_2_out = {{20{ID_IR[31]}}, {ID_IR[31:25], ID_IR[11:7]}};  // Bit_Extender bit_extender_2
  // Probe on ID_PC[11:0]
  // Probe on EX_PC[11:0]
  \单周期硬布线控制器  \u_单周期硬布线控制器_1  (
    .Funct({ID_IR[30], ID_IR[25], ID_IR[14:12]}), .OP(ID_IR[6:2]), .ALU_OP(\单周期硬布线控制器_1_alu_op ),
    .MemToReg(\单周期硬布线控制器_1_memtoreg ), .MemWrite(\单周期硬布线控制器_1_memwrite ), .ALU_SRC(\单周期硬布线控制器_1_alu_src ),
    .RegWrite(\单周期硬布线控制器_1_regwrite ), .ecall(\单周期硬布线控制器_1_ecall ), .S_type(\单周期硬布线控制器_1_s_type [0]),
    .Jalr(\单周期硬布线控制器_1_jalr ), .Beq(\单周期硬布线控制器_1_beq ), .JAL(\单周期硬布线控制器_1_jal ), .Bne(\单周期硬布线控制器_1_bne ),
    .in_3(ID_IR[21]), .uret(\单周期硬布线控制器_1_uret ), .U_Type(\单周期硬布线控制器_1_s_type [1]), .BLTU(\单周期硬布线控制器_1_bltu ));
  Multiplexer #(.select(2), .width(32), .disabled("Z"), .enable("false")) multiplexer_4 (
    .in0(bit_extender_1_out), .in1(bit_extender_2_out), .in2({ID_IR[31:12], {12{1'b0}}}),
    .out(multiplexer_4_out), .sel(\单周期硬布线控制器_1_s_type ));  // open: in3
  // Probe on M_PC[11:0]
  D_Flip_Flop #(.trigger("high"), .Pre_Clr_Positions("LEGACY"), .NegatePresetClear("false"), .enable("true"), .NewFFLayout("false")) d_ff_1 (.Q(d_ff_1_q));  // open: clk, D, Qn, preset, en, reset
  // Probe on 13'h5bc
  assign bit_extender_3_out = {{20{ID_IR[31]}}, {ID_IR[31], ID_IR[7], ID_IR[30:25], ID_IR[11:8]}};  // Bit_Extender bit_extender_3
  assign bit_extender_4_out = {{12{ID_IR[31]}}, {ID_IR[31], ID_IR[19:12], ID_IR[20], ID_IR[30:21]}};  // Bit_Extender bit_extender_4
  // Probe on WB_PC[11:0]
  Comparator #(.width(13), .mode("twosComplement")) comparator_1 (
    .a(CNT_num), .b(13'h5bc), .eq(comparator_1_eq), .lt(comparator_1_lt));  // open: gt
  Clock #(.highDuration(1), .lowDuration(1)) clock_1 (.out(clock_1_out));
  Regifile_FailingEdge regifile_failingedge_1 (
    .Din(RDin), .Clk(CLK), .R1(regifile_failingedge_1_r1), .R2(regifile_failingedge_1_r2), .WE(RegWrite),
    .W_num(undriven), .R1_num(multiplexer_2_out), .R2_num(multiplexer_3_out));
  Shifter #(.width(32), .shift("ll")) shifter_1 (.in(bit_extender_3_out), .\dist (5'b00001), .out(shifter_1_out));
  Shifter #(.width(32), .shift("ll")) shifter_2 (.in(bit_extender_4_out), .\dist (5'b00001), .out(shifter_2_out));
  nand nand_1 (nand_1_out, d_ff_1_q, comparator_1_eq);
  Counter #(.width(13), .max('h1fff), .ongoal("stay"), .trigger("rising"), .behavior("old")) counter_1 (
    .count(comparator_1_lt), .Q(CNT_num), .clk(clock_1_out));  // open: load, D, carry, clr, preset
  or or_3 (or_3_out, DataCorrelate, RST);
  assign CLK = nand_1_out ? clock_1_out : 1'bz;  // Controlled_Buffer controlled_buffer_1
  or or_4 (or_4_out, undriven_14, or_5_out, undriven_13);
  Priority_Encoder #(.select(2), .disabled("Z")) priority_encoder_1 (
    .in0(1'b1), .in1(undriven_13), .in2(or_5_out), .in3(undriven_14), .out(priority_encoder_1_out));  // open: gs, en_out, en_in
  Pull_Resistor #(.pull(1)) pull_resistor_1 (.node(CLK));
  Comparator #(.width(32), .mode("twosComplement")) comparator_2 (
    .a(undriven_7), .b(32'h22), .eq(comparator_2_eq));  // open: gt, lt
  not not_2 (not_2_out, comparator_2_eq);
  not not_3 (not_3_out, halt);
  or or_5 (or_5_out, and_4_out, and_5_out, and_1_out);
  and and_1 (and_1_out, undriven_2, alu_1_equal);
  Multiplexer #(.select(1), .width(32), .disabled("Z"), .enable("false")) multiplexer_5 (
    .in0(undriven_8), .in1(undriven_9), .out(multiplexer_5_out), .sel(undriven_4));
  Register #(.width(32), .trigger("rising"), .Select("low")) register_1 (
    .D(undriven_8), .en(and_2_out), .Q(LedData), .clk(CLK));  // open: clr
  and and_2 (and_2_out, comparator_2_eq, undriven_6);
  and and_3 (and_3_out, not_2_out, undriven_6);
  Counter #(.width(16), .max('hffff), .ongoal("wrap"), .trigger("rising"), .behavior("new")) counter_2 (
    .count(not_3_out), .Q(\总周期数 ), .clk(CLK));  // open: load, D, carry, clr, preset, down
  and and_4 (and_4_out, undriven_16, alu_1_out_6);
  and and_5 (and_5_out, undriven_15, not_4_out);
  not not_4 (not_4_out, alu_1_equal);
  ALU alu_1 (
    .X(undriven_7), .Y(multiplexer_5_out), .AluOP(undriven_3), .Equal(alu_1_equal), .Result(alu_1_result),
    .out_6(alu_1_out_6));  // open: Result_2, out_4
  Adder #(.width(32)) adder_2 (.a(EX_PC), .b(undriven_11), .out(adder_2_out));  // open: cin, cout
  Adder #(.width(32)) adder_3 (.a(EX_PC), .b(undriven_12), .out(adder_3_out));  // open: cin, cout
  RAM #(.addrWidth(10), .dataWidth(32), .bus("separate"), .Select("high")) ram_1 (
    .addr(undriven_19), .din(MDin), .data(ram_1_data), .str(MemWrite), .sel(1'b1), .clk(CLK), .ld(1'b1),
    .clr(RST));
  or or_6 (undriven_26[1], undriven_21, undriven_20);
  Multiplexer #(.select(2), .width(32), .disabled("Z"), .enable("false")) multiplexer_6 (
    .in0(undriven_24), .in1(undriven_23), .in2(undriven_25), .out(RDin), .sel(undriven_26));  // open: in3
  Multiplexer #(.select(1), .width(1), .disabled("Z"), .enable("false")) multiplexer_7 (
    .in0(undriven_22), .in1(1'b0), .out(halt), .sel(Go));

  // Other names for the same wires on the sheet: MEM_PC[31:0] = M_PC

  // Notes on the sheet:
  //   中断源
  //   时空图监测，可删除
  //   中断等待指示
  //   BranchAddr
  //   BranchChoice
  //   数码管输出
  //   取指
  //   指令存储器
  //   contents of rom_1 (hex, n*v repeats v):
  //   100493 100006f 100493 200913 300993 100006f 100493 200913 300993 100006f 100493 200913 300993
  //   100006f 100493 200913 300993 29c000ef 100413 100493 1f49493 900533 2200893 73 24d493 48463 fedff06f
  //   900533 2200893 73 100493 249493 900533 2200893 73 48463 fedff06f 100493 1f49493 900533 2200893 73
  //   4034d493 900533 2200893 73 4044d493 900533 2200893 73 4044d493 900533 2200893 73 4044d493 900533
  //   2200893 73 4044d493 900533 2200893 73 4044d493 900533 2200893 73 4044d493 900533 2200893 73 4044d493
  //   900533 2200893 73 100413 1f41993 41f9d993 433 c00913 300b13 140413 f47413 800293 100313 499993
  //   89e9b3 1300533 2200893 73 406282b3 fe0294e3 140413 f00f93 1f47433 1c41413 800293 100313 49d993
  //   89e9b3 1300533 2200893 73 406282b3 fe0294e3 1c45413 406b0b33 b0463 f95ff06f 2b3 fff2c293 829293
  //   ff2e293 500533 2200893 73 fff00413 493 84a023 140413 448493 84a023 140413 448493 84a023 140413
  //   448493 84a023 140413 448493 84a023 140413 448493 84a023 140413 448493 84a023 140413 448493 84a023
  //   140413 448493 84a023 140413 448493 84a023 140413 448493 84a023 140413 448493 84a023 140413 448493
  //   84a023 140413 448493 84a023 140413 448493 84a023 140413 448493 84a023 140413 448493 140413 433
  //   3c00493 42983 4aa03 149a2b3 28663 134a023 1442023 ffc48493 fe9412e3 800533 2200893 73 440413 3c00493
  //   fc9416e3 a00893 73 413 140413 800533 2200893 73 240413 800533 2200893 73 340413 800533 2200893 73
  //   440413 800533 2200893 73 540413 800533 2200893 73 640413 800533 2200893 73 740413 800533 2200893 73
  //   840413 800533 2200893 2200893 73 8067
  //   指令探针
  //   分支冲突
  //   rs1
  //   rs2
  //   I
  //   S
  //   JAL
  //   JALR
  //   URET
  //   *U:imm[31:12]
  //   控制位
  //   译码
  //   Beq
  //   Bne
  //   BLTU
  //   MemToReg
  //   MemWrite
  //   AluOP
  //   AluSrcB
  //   RegWrite
  //   U_type
  //   S_type
  //   rd
  //   B:imm[12:0]
  //   J:imm[20:0]
  //   流水调试日志用
  //   暂停节拍，不能为0
  //   WriteBackData
  //   WriteReg#
  //   戳工具置1进入计数暂停模式，ctrl+k时钟自动运行到对应节拍暂停
  //   ctrl+k关闭时钟连续运行，将控制位置零，进入单步调试模式调试
  //   可计数暂停的时钟源
  //   BranchTaken
  //   BranchChoice
  //   执行
  //   BranchAddr
  //   为方便自动评测，需要输出流水线各段保存的PC值，注意是PC不是PC+4，另外ID段寄存器写入信息，Mem段内存写入信息也要输出
  //   ALU_result
  //   访存
  //   数据存储器
  //   ALU_result
  //   Data
  //   写回
  //   MemToReg
  //   WriteBackData
  //   WriteReg#
  //   JAL or JALR
endmodule

module \重定向流水线  (
  output RegWrite,
  output MemWrite,
  output [31:0] IF_PC,
  output [31:0] ID_PC,
  output [31:0] EX_PC,
  output [31:0] M_PC,
  output [31:0] WB_PC,
  output [31:0] RDin,
  output [31:0] MDin,
  output [31:0] LedData
);

  wire alu_1_equal, alu_1_out_6, and_1_out, and_2_out, and_3_out, and_4_out, and_5_out, CLK, clock_1_out,
       comparator_1_eq, comparator_1_lt, comparator_2_eq, d_ff_1_q, Go, halt, IR1, IR2, IR3, LoadUse,
       nand_1_out, not_1_out, not_2_out, not_3_out, not_4_out, or_1_out, or_3_out, or_4_out, or_5_out,
       riscv_probe_4_p5, riscv_probe_4_p9, RST, undriven_3, undriven_4, undriven_6, undriven_7, undriven_8,
       undriven_17, undriven_18, undriven_19, undriven_20, undriven_22, undriven_23, undriven_24,
       undriven_25, W1, W2, W3, \单周期硬布线控制器_1_alu_src , \单周期硬布线控制器_1_beq , \单周期硬布线控制器_1_bltu ,
       \单周期硬布线控制器_1_bne , \单周期硬布线控制器_1_ecall , \单周期硬布线控制器_1_jal , \单周期硬布线控制器_1_jalr , \单周期硬布线控制器_1_memtoreg ,
       \单周期硬布线控制器_1_memwrite , \单周期硬布线控制器_1_regwrite , \单周期硬布线控制器_1_uret , \源寄存器使用情况_1_rs1_used ,
       \源寄存器使用情况_1_rs2_used ;
  wire [1:0] priority_encoder_1_out, undriven_2, undriven_16, undriven_29, \单周期硬布线控制器_1_s_type ,
       \数据相关检测_rs1fwd , \数据相关检测_rs2fwd ;
  wire [3:0] undriven_5, \单周期硬布线控制器_1_alu_op ;
  wire [4:0] multiplexer_2_out, multiplexer_3_out, undriven, undriven_12, undriven_21;
  wire [12:0] CNT_num;
  wire [15:0] \LoadUse次数 , \总周期数 , \插入气泡数 , \无条件分支数 , \条件分支成功数 ;
  wire [31:0] adder_2_out, adder_3_out, alu_1_result, bit_extender_1_out, bit_extender_2_out,
       bit_extender_3_out, bit_extender_4_out, EX_IR, ID_IR, IF_IR, MEM_IR, multiplexer_1_out,
       multiplexer_4_out, multiplexer_5_out, multiplexer_6_out, multiplexer_7_out, ram_1_data,
       regifile_failingedge_1_r1, regifile_failingedge_1_r2, riscv_probe_4_p4, shifter_1_out, shifter_2_out,
       undriven_9, undriven_10, undriven_11, undriven_13, undriven_14, undriven_15, undriven_26, undriven_27,
       undriven_28, WB_IR;

  Button \u_总复位  (.out(RST));
  Button _1 (.out(IR1));
  Button _2 (.out(IR2));
  Button _3 (.out(IR3));
  // Probe on \总周期数 
  // Probe on \总周期数 
  Button \u_继续运行  (.out(Go));
  LED #(.active("true")) led_1 (.in(W1));
  LED #(.active("true")) led_2 (.in(W2));
  LED #(.active("true")) led_3 (.in(W3));
  Hex_Digit_Display hex_digit_display_1 (.value(LedData[31:28]));  // open: dp
  // Probe on IF_PC[19:0]
  // RiscV_Probe riscv_probe_1: pin names not known; wires that end beside it: IF_IR
  Hex_Digit_Display hex_digit_display_2 (.value(LedData[23:20]));  // open: dp
  Hex_Digit_Display hex_digit_display_3 (.value(LedData[27:24]));  // open: dp
  // Probe on ID_PC[19:0]
  // RiscV_Probe riscv_probe_2: pin names not known; wires that end beside it: ID_IR
  Multiplexer #(.select(2), .width(32), .disabled("Z"), .enable("false")) multiplexer_1 (
    .in0(riscv_probe_4_p4), .in1(alu_1_result), .in2(adder_2_out), .in3(adder_3_out),
    .out(multiplexer_1_out), .sel(priority_encoder_1_out));
  not not_1 (not_1_out, or_1_out);
  or or_1 (or_1_out, LoadUse, halt);
  Hex_Digit_Display hex_digit_display_4 (.value(LedData[15:12]));  // open: dp
  Hex_Digit_Display hex_digit_display_5 (.value(LedData[19:16]));  // open: dp
  Register #(.width(32), .trigger("rising"), .Select("low")) PC (
    .D(multiplexer_1_out), .en(not_1_out), .Q(IF_PC), .clk(CLK), .clr(RST));
  Hex_Digit_Display hex_digit_display_6 (.value(LedData[7:4]));  // open: dp
  Hex_Digit_Display hex_digit_display_7 (.value(LedData[11:8]));  // open: dp
  // Probe on EX_PC[19:0]
  // RiscV_Probe riscv_probe_3: pin names not known; wires that end beside it: EX_IR
  Hex_Digit_Display hex_digit_display_8 (.value(LedData[3:0]));  // open: dp
  ROM #(.addrWidth(10), .dataWidth(32), .Select("high")) rom_1 (.addr(IF_PC[11:2]), .data(IF_IR));
  // RiscV_Probe riscv_probe_4: pin names not known; wires that end beside it: IF_IR, IF_IR, IF_PC, riscv_probe_4_p4, riscv_probe_4_p5, CLK, ID_IR, ID_PC, riscv_probe_4_p9, RST, ID_IR[31:20], {ID_IR[31:25], ID_IR[11:7]}, ID_IR[31:12]
  Adder #(.width(32)) adder_1 (.a(IF_PC), .b(32'h4), .out(riscv_probe_4_p4));  // open: cin, cout
  // Probe on \总周期数 
  // Probe on M_PC[19:0]
  // RiscV_Probe riscv_probe_5: pin names not known; wires that end beside it: MEM_IR
  or or_2 (riscv_probe_4_p5, LoadUse, halt);
  // Probe on \总周期数 
  // Probe on \无条件分支数 
  // Probe on \条件分支成功数 
  // Probe on \插入气泡数 
  // Probe on \LoadUse次数 
  \源寄存器使用情况  \u_源寄存器使用情况_1  (
    .OP(ID_IR[6:2]), .Funct({ID_IR[30], ID_IR[25], ID_IR[14:12]}), .rs1_used(\源寄存器使用情况_1_rs1_used ),
    .rs2_used(\源寄存器使用情况_1_rs2_used ));
  // Probe on IF_PC[11:0]
  // Probe on WB_PC[19:0]
  // RiscV_Probe riscv_probe_6: pin names not known; wires that end beside it: WB_IR
  \数据相关检测  \u_数据相关检测  (
    .rs1(multiplexer_2_out), .rs2(multiplexer_3_out), .rs1_used(\源寄存器使用情况_1_rs1_used ),
    .EX_RegWrite(undriven_7), .EX_rd(undriven_12), .rs2_used(\源寄存器使用情况_1_rs2_used ),
    .MEM_RegWrite(undriven_22), .MEM_rd(undriven_21), .rs1Fwd(\数据相关检测_rs1fwd ), .rs2Fwd(\数据相关检测_rs2fwd ),
    .EX_MemToReg(undriven_4), .LoadUse(LoadUse));  // open: DataCorrelate
  Multiplexer #(.select(1), .width(5), .disabled("Z"), .enable("false")) multiplexer_2 (
    .in0(ID_IR[19:15]), .in1(5'b10001), .out(multiplexer_2_out), .sel(\单周期硬布线控制器_1_ecall ));
  Multiplexer #(.select(1), .width(5), .disabled("Z"), .enable("false")) multiplexer_3 (
    .in0(ID_IR[24:20]), .in1(5'b01010), .out(multiplexer_3_out), .sel(\单周期硬布线控制器_1_ecall ));
  assign bit_extender_1_out = {{20{ID_IR[31]}}, ID_IR[31:20]};  // Bit_Extender bit_extender_1
  assign bit_extender_2_out = {{20{ID_IR[31]}}, {ID_IR[31:25], ID_IR[11:7]}};  // Bit_Extender bit_extender_2
  // Probe on EX_PC[11:0]
  // Probe on ID_PC[11:0]
  \单周期硬布线控制器  \u_单周期硬布线控制器_1  (
    .Funct({ID_IR[30], ID_IR[25], ID_IR[14:12]}), .OP(ID_IR[6:2]), .ALU_OP(\单周期硬布线控制器_1_alu_op ),
    .MemToReg(\单周期硬布线控制器_1_memtoreg ), .MemWrite(\单周期硬布线控制器_1_memwrite ), .ALU_SRC(\单周期硬布线控制器_1_alu_src ),
    .RegWrite(\单周期硬布线控制器_1_regwrite ), .ecall(\单周期硬布线控制器_1_ecall ), .S_type(\单周期硬布线控制器_1_s_type [0]),
    .Jalr(\单周期硬布线控制器_1_jalr ), .Beq(\单周期硬布线控制器_1_beq ), .JAL(\单周期硬布线控制器_1_jal ), .Bne(\单周期硬布线控制器_1_bne ),
    .in_3(ID_IR[21]), .uret(\单周期硬布线控制器_1_uret ), .U_Type(\单周期硬布线控制器_1_s_type [1]), .BLTU(\单周期硬布线控制器_1_bltu ));
  Multiplexer #(.select(2), .width(32), .disabled("Z"), .enable("false")) multiplexer_4 (
    .in0(bit_extender_1_out), .in1(bit_extender_2_out), .in2({ID_IR[31:12], {12{1'b0}}}),
    .out(multiplexer_4_out), .sel(\单周期硬布线控制器_1_s_type ));  // open: in3
  // Probe on M_PC[11:0]
  D_Flip_Flop #(.trigger("high"), .Pre_Clr_Positions("LEGACY"), .NegatePresetClear("false"), .enable("true"), .NewFFLayout("false")) d_ff_1 (.Q(d_ff_1_q));  // open: clk, D, Qn, preset, en, reset
  // Probe on 13'h33d
  assign bit_extender_3_out = {{20{ID_IR[31]}}, {ID_IR[31], ID_IR[7], ID_IR[30:25], ID_IR[11:8]}};  // Bit_Extender bit_extender_3
  assign bit_extender_4_out = {{12{ID_IR[31]}}, {ID_IR[31], ID_IR[19:12], ID_IR[20], ID_IR[30:21]}};  // Bit_Extender bit_extender_4
  // Probe on WB_PC[11:0]
  Comparator #(.width(13), .mode("twosComplement")) comparator_1 (
    .a(CNT_num), .b(13'h33d), .eq(comparator_1_eq), .lt(comparator_1_lt));  // open: gt
  Clock #(.highDuration(1), .lowDuration(1)) clock_1 (.out(clock_1_out));
  Regifile_FailingEdge regifile_failingedge_1 (
    .Din(RDin), .Clk(CLK), .R1(regifile_failingedge_1_r1), .R2(regifile_failingedge_1_r2), .WE(RegWrite),
    .W_num(undriven), .R1_num(multiplexer_2_out), .R2_num(multiplexer_3_out));
  Shifter #(.width(32), .shift("ll")) shifter_1 (.in(bit_extender_3_out), .\dist (5'b00001), .out(shifter_1_out));
  Shifter #(.width(32), .shift("ll")) shifter_2 (.in(bit_extender_4_out), .\dist (5'b00001), .out(shifter_2_out));
  nand nand_1 (nand_1_out, d_ff_1_q, comparator_1_eq);
  Counter #(.width(13), .max('h1fff), .ongoal("stay"), .trigger("rising"), .behavior("old")) counter_1 (
    .count(comparator_1_lt), .Q(CNT_num), .clk(clock_1_out));  // open: load, D, carry, clr, preset
  or or_3 (or_3_out, LoadUse, RST);
  assign CLK = nand_1_out ? clock_1_out : 1'bz;  // Controlled_Buffer controlled_buffer_1
  or or_4 (or_4_out, undriven_18, or_5_out, undriven_17);
  Priority_Encoder #(.select(2), .disabled("Z")) priority_encoder_1 (
    .in0(1'b1), .in1(undriven_17), .in2(or_5_out), .in3(undriven_18), .out(priority_encoder_1_out));  // open: gs, en_out, en_in
  Multiplexer #(.select(2), .width(32), .disabled("Z"), .enable("false")) multiplexer_5 (
    .in0(undriven_9), .in1(undriven_15), .in2(RDin), .out(multiplexer_5_out), .sel(undriven_2));  // open: in3
  Multiplexer #(.select(2), .width(32), .disabled("Z"), .enable("false")) multiplexer_6 (
    .in0(undriven_10), .in1(undriven_15), .in2(RDin), .out(multiplexer_6_out), .sel(undriven_16));  // open: in3
  Pull_Resistor #(.pull(1)) pull_resistor_1 (.node(CLK));
  Comparator #(.width(32), .mode("twosComplement")) comparator_2 (
    .a(multiplexer_5_out), .b(32'h22), .eq(comparator_2_eq));  // open: gt, lt
  not not_2 (not_2_out, comparator_2_eq);
  not not_3 (not_3_out, halt);
  or or_5 (or_5_out, and_5_out, and_4_out, and_1_out);
  and and_1 (and_1_out, undriven_3, alu_1_equal);
  Multiplexer #(.select(1), .width(32), .disabled("Z"), .enable("false")) multiplexer_7 (
    .in0(multiplexer_6_out), .in1(undriven_11), .out(multiplexer_7_out), .sel(undriven_6));
  Register #(.width(32), .trigger("rising"), .Select("low")) register_1 (
    .D(multiplexer_6_out), .en(and_2_out), .Q(LedData), .clk(CLK));  // open: clr
  and and_2 (and_2_out, comparator_2_eq, undriven_8);
  and and_3 (and_3_out, not_2_out, undriven_8);
  Counter #(.width(16), .max('hffff), .ongoal("wrap"), .trigger("rising"), .behavior("new")) counter_2 (
    .count(not_3_out), .Q(\总周期数 ), .clk(CLK));  // open: load, D, carry, clr, preset, down
  and and_4 (and_4_out, undriven_19, not_4_out);
  and and_5 (and_5_out, undriven_20, alu_1_out_6);
  not not_4 (not_4_out, alu_1_equal);
  ALU alu_1 (
    .X(multiplexer_5_out), .Y(multiplexer_7_out), .AluOP(undriven_5), .Equal(alu_1_equal),
    .Result(alu_1_result), .out_6(alu_1_out_6));  // open: Result_2, out_4
  Adder #(.width(32)) adder_2 (.a(EX_PC), .b(undriven_13), .out(adder_2_out));  // open: cin, cout
  Adder #(.width(32)) adder_3 (.a(EX_PC), .b(undriven_14), .out(adder_3_out));  // open: cin, cout
  RAM #(.addrWidth(10), .dataWidth(32), .bus("separate"), .Select("high")) ram_1 (
    .addr(undriven_15[11:2]), .din(MDin), .data(ram_1_data), .str(MemWrite), .sel(1'b1), .clk(CLK),
    .ld(1'b1), .clr(RST));
  or or_6 (undriven_29[1], undriven_24, undriven_23);
  Multiplexer #(.select(2), .width(32), .disabled("Z"), .enable("false")) multiplexer_8 (
    .in0(undriven_27), .in1(undriven_26), .in2(undriven_28), .out(RDin), .sel(undriven_29));  // open: in3
  Multiplexer #(.select(1), .width(1), .disabled("Z"), .enable("false")) multiplexer_9 (
    .in0(undriven_25), .in1(1'b0), .out(halt), .sel(Go));

  // Other names for the same wires on the sheet: MEM_PC[31:0] = M_PC

  // Notes on the sheet:
  //   中断源
  //   时空图监测，可删除
  //   中断等待指示
  //   BranchAddr
  //   BranchChoice
  //   数码管输出
  //   取指
  //   指令存储器
  //   contents of rom_1 (hex, n*v repeats v):
  //   100493 100006f 100493 200913 300993 100006f 100493 200913 300993 100006f 100493 200913 300993
  //   100006f 100493 200913 300993 29c000ef 100413 100493 1f49493 900533 2200893 73 24d493 48463 fedff06f
  //   900533 2200893 73 100493 249493 900533 2200893 73 48463 fedff06f 100493 1f49493 900533 2200893 73
  //   4034d493 900533 2200893 73 4044d493 900533 2200893 73 4044d493 900533 2200893 73 4044d493 900533
  //   2200893 73 4044d493 900533 2200893 73 4044d493 900533 2200893 73 4044d493 900533 2200893 73 4044d493
  //   900533 2200893 73 100413 1f41993 41f9d993 433 c00913 300b13 140413 f47413 800293 100313 499993
  //   89e9b3 1300533 2200893 73 406282b3 fe0294e3 140413 f00f93 1f47433 1c41413 800293 100313 49d993
  //   89e9b3 1300533 2200893 73 406282b3 fe0294e3 1c45413 406b0b33 b0463 f95ff06f 2b3 fff2c293 829293
  //   ff2e293 500533 2200893 73 fff00413 493 84a023 140413 448493 84a023 140413 448493 84a023 140413
  //   448493 84a023 140413 448493 84a023 140413 448493 84a023 140413 448493 84a023 140413 448493 84a023
  //   140413 448493 84a023 140413 448493 84a023 140413 448493 84a023 140413 448493 84a023 140413 448493
  //   84a023 140413 448493 84a023 140413 448493 84a023 140413 448493 84a023 140413 448493 140413 433
  //   3c00493 42983 4aa03 149a2b3 28663 134a023 1442023 ffc48493 fe9412e3 800533 2200893 73 440413 3c00493
  //   fc9416e3 a00893 73 413 140413 800533 2200893 73 240413 800533 2200893 73 340413 800533 2200893 73
  //   440413 800533 2200893 73 540413 800533 2200893 73 640413 800533 2200893 73 740413 800533 2200893 73
  //   840413 800533 2200893 2200893 73 8067
  //   指令探针
  //   分支冲突
  //   rs1
  //   rs2
  //   I
  //   S
  //   JAL
  //   JALR
  //   URET
  //   *U:imm[31:12]
  //   控制位
  //   译码
  //   Beq
  //   Bne
  //   BLTU
  //   MemToReg
  //   MemWrite
  //   AluOP
  //   AluSrcB
  //   RegWrite
  //   U_type
  //   S_type
  //   rd
  //   B:imm[12:0]
  //   J:imm[20:0]
  //   流水调试日志用
  //   暂停节拍，不能为0
  //   WriteBackData
  //   WriteReg#
  //   戳工具置1进入计数暂停模式，ctrl+k时钟自动运行到对应节拍暂停
  //   ctrl+k关闭时钟连续运行，将控制位置零，进入单步调试模式调试
  //   可计数暂停的时钟源
  //   BranchTaken
  //   BranchChoice
  //   重定向
  //   执行
  //   BranchAddr
  //   为方便自动评测，需要输出流水线各段保存的PC值，注意是PC不是PC+4，另外ID段寄存器写入信息，Mem段内存写入信息也要输出
  //   ALU_result
  //   访存
  //   数据存储器
  //   ALU_result
  //   Data
  //   写回
  //   MemToReg
  //   WriteBackData
  //   WriteReg#
  //   JAL or JALR
endmodule

module \中断按键参考电路  (
  input  \同步清零信号 ,
  output \与中断屏蔽位与 
);

  wire \_1号中断_out , and_1_out, clock_1_out, d_ff_1_q, or_1_out, or_2_out;

  Clock #(.highDuration(1), .lowDuration(1)) clock_1 (.out(clock_1_out));
  Button \_1号中断  (.out(\_1号中断_out ));
  LED #(.active("true")) \_1号中断等待指示灯  (.in(or_1_out));
  or or_1 (or_1_out, \与中断屏蔽位与 , d_ff_1_q);
  D_Flip_Flop #(.trigger("rising"), .Pre_Clr_Positions("LEGACY"), .NegatePresetClear("false"), .enable("true"), .NewFFLayout("false")) d_ff_1 (
    .clk(\_1号中断_out ), .D(1'b1), .Q(d_ff_1_q), .reset(\与中断屏蔽位与 ));  // open: Qn, preset, en
  or or_2 (or_2_out, d_ff_1_q, \与中断屏蔽位与 );
  and and_1 (and_1_out, or_2_out, ~\同步清零信号 );  // AND_Gate
  D_Flip_Flop #(.trigger("rising"), .Pre_Clr_Positions("LEGACY"), .NegatePresetClear("false"), .enable("true"), .NewFFLayout("false")) IR1 (
    .clk(clock_1_out), .D(and_1_out), .Q(\与中断屏蔽位与 ));  // open: Qn, preset, en, reset

  // Notes on the sheet:
  //   中断信号采样参考电路
  //   Reset 
endmodule

module \单周期_单级中断  (
  input  IR1,
  input  IR2,
  input  IR3,
  output RegWrite,
  output MemWrite,
  output [31:0] PC,
  output [31:0] IR,
  output [31:0] RDin,
  output [31:0] MDin,
  output [31:0] LedData
);

  wire CLK, clock_1_out, comparator_1_eq, comparator_2_eq, comparator_3_eq, comparator_4_eq, comparator_5_eq,
       comparator_5_lt, d_ff_1_q, Go, IR1_t, IR2_t, IR3_t, IRA, IRB, IRC, nand_1_out, or_1_out, W1, W2, W3;
  wire [12:0] CNT_num;
  wire [15:0] \总周期数 ;

  Button \u_继续运行  (.out(Go));
  Button _1 ();  // open: out
  Button _2 ();  // open: out
  Button _3 ();  // open: out
  LED #(.active("true")) led_1 (.in(W1));
  LED #(.active("true")) led_2 (.in(W2));
  LED #(.active("true")) led_3 (.in(W3));
  Hex_Digit_Display hex_digit_display_1 (.value(LedData[31:28]));  // open: dp
  Comparator #(.width(16), .mode("twosComplement")) comparator_1 (
    .a(16'h23b), .b(\总周期数 ), .eq(comparator_1_eq));  // open: gt, lt
  Comparator #(.width(16), .mode("twosComplement")) comparator_2 (
    .a(\总周期数 ), .b(16'h1), .eq(comparator_2_eq));  // open: gt, lt
  Comparator #(.width(16), .mode("twosComplement")) comparator_3 (
    .a(\总周期数 ), .b(16'h4), .eq(comparator_3_eq));  // open: gt, lt
  Comparator #(.width(16), .mode("twosComplement")) comparator_4 (
    .a(\总周期数 ), .b(16'h7), .eq(comparator_4_eq));  // open: gt, lt
  Hex_Digit_Display hex_digit_display_2 (.value(LedData[27:24]));  // open: dp
  Hex_Digit_Display hex_digit_display_3 (.value(LedData[23:20]));  // open: dp
  or or_1 (or_1_out, comparator_1_eq, comparator_2_eq);
  assign IRA = or_1_out ? ~CLK : 1'bz;  // Controlled_Inverter controlled_inverter_1
  assign IRB = comparator_3_eq ? ~CLK : 1'bz;  // Controlled_Inverter controlled_inverter_2
  assign IRC = comparator_4_eq ? ~CLK : 1'bz;  // Controlled_Inverter controlled_inverter_3
  Hex_Digit_Display hex_digit_display_4 (.value(LedData[19:16]));  // open: dp
  Hex_Digit_Display hex_digit_display_5 (.value(LedData[15:12]));  // open: dp
  Pull_Resistor #(.pull(0)) pull_resistor_1 (.node(IRA));
  Pull_Resistor #(.pull(0)) pull_resistor_2 (.node(IRB));
  Pull_Resistor #(.pull(0)) pull_resistor_3 (.node(IRC));
  Hex_Digit_Display hex_digit_display_6 (.value(LedData[7:4]));  // open: dp
  Hex_Digit_Display hex_digit_display_7 (.value(LedData[11:8]));  // open: dp
  // Probe on \总周期数 
  Hex_Digit_Display hex_digit_display_8 (.value(LedData[3:0]));  // open: dp
  or or_2 (IR1_t, IR1, IRA);
  or or_3 (IR2_t, IR2, IRB);
  or or_4 (IR3_t, IR3, IRC);
  D_Flip_Flop #(.trigger("high"), .Pre_Clr_Positions("LEGACY"), .NegatePresetClear("false"), .enable("true"), .NewFFLayout("false")) d_ff_1 (.Q(d_ff_1_q));  // open: clk, D, Qn, preset, en, reset
  // Probe on 13'hc
  Comparator #(.width(13), .mode("twosComplement")) comparator_5 (
    .a(CNT_num), .b(13'hc), .eq(comparator_5_eq), .lt(comparator_5_lt));  // open: gt
  Clock #(.highDuration(1), .lowDuration(1)) clock_1 (.out(clock_1_out));
  Counter #(.width(13), .max('h1fff), .ongoal("stay"), .trigger("rising"), .behavior("old")) counter_1 (
    .count(comparator_5_lt), .Q(CNT_num), .clk(clock_1_out));  // open: load, D, carry, clr, preset
  nand nand_1 (nand_1_out, d_ff_1_q, comparator_5_eq);
  assign CLK = nand_1_out ? clock_1_out : 1'bz;  // Controlled_Buffer controlled_buffer_1
  Pull_Resistor #(.pull(1)) pull_resistor_4 (.node(CLK));

  // Notes on the sheet:
  //   中断源
  //   中断等待指示
  //   总复位信号应将除ROM以外所有存储组件全部清零
  //   单级中断测试信号模拟器
  //   数码管输出
  //   数码管输出应该用寄存器锁存，否则显示数据只能一闪而过
  //   为方便自动评测，需要输出PC，IR，寄存器堆写如数据RDin
  //   RAM写使能MemWrite、RAM写入数据MDin等信号
  //   控制位
  //   暂停节拍，不能为0
  //   戳工具置1进入计数暂停模式，ctrl+k时钟自动运行到对应节拍暂停
  //   ctrl+k关闭时钟连续运行，将控制位置零，进入单步调试模式调试
  //   可计数暂停的时钟源
endmodule

module \单周期_多级中断  (
  input  IR1,
  input  IR2,
  input  IR3,
  output RegWrite,
  output MemWrite,
  output [31:0] PC,
  output [31:0] IR,
  output [31:0] RDin,
  output [31:0] MDin,
  output [31:0] LedData
);

  wire CLK, clock_1_out, comparator_1_eq, comparator_2_eq, comparator_3_eq, comparator_4_eq, comparator_5_eq,
       comparator_6_eq, comparator_6_lt, d_ff_1_q, Go, IR1_t, IR2_t, IR3_t, IRA, IRB, IRC, nand_1_out,
       or_1_out, or_2_out, W1, W2, W3;
  wire [12:0] CNT_num;
  wire [15:0] \总周期数 ;

  Button \u_继续运行  (.out(Go));
  Button _1 ();  // open: out
  Button _2 ();  // open: out
  Button _3 ();  // open: out
  LED #(.active("true")) led_1 (.in(W1));
  LED #(.active("true")) led_2 (.in(W2));
  LED #(.active("true")) led_3 (.in(W3));
  Hex_Digit_Display hex_digit_display_1 (.value(LedData[31:28]));  // open: dp
  Comparator #(.width(16), .mode("twosComplement")) comparator_1 (
    .a(\总周期数 ), .b(16'h7), .eq(comparator_1_eq));  // open: gt, lt
  Comparator #(.width(16), .mode("twosComplement")) comparator_2 (
    .a(\总周期数 ), .b(16'h241), .eq(comparator_2_eq));  // open: gt, lt
  Hex_Digit_Display hex_digit_display_2 (.value(LedData[27:24]));  // open: dp
  Hex_Digit_Display hex_digit_display_3 (.value(LedData[23:20]));  // open: dp
  Comparator #(.width(16), .mode("twosComplement")) comparator_3 (
    .a(16'h258), .b(\总周期数 ), .eq(comparator_3_eq));  // open: gt, lt
  or or_1 (or_1_out, comparator_3_eq, comparator_4_eq);
  Comparator #(.width(16), .mode("twosComplement")) comparator_4 (
    .a(\总周期数 ), .b(16'h1), .eq(comparator_4_eq));  // open: gt, lt
  Comparator #(.width(16), .mode("twosComplement")) comparator_5 (
    .a(\总周期数 ), .b(16'h4), .eq(comparator_5_eq));  // open: gt, lt
  or or_2 (or_2_out, comparator_1_eq, comparator_2_eq);
  Hex_Digit_Display hex_digit_display_4 (.value(LedData[15:12]));  // open: dp
  Hex_Digit_Display hex_digit_display_5 (.value(LedData[19:16]));  // open: dp
  Pull_Resistor #(.pull(0)) pull_resistor_1 (.node(IRA));
  assign IRA = or_1_out ? ~CLK : 1'bz;  // Controlled_Inverter controlled_inverter_1
  Pull_Resistor #(.pull(0)) pull_resistor_2 (.node(IRB));
  assign IRB = comparator_5_eq ? ~CLK : 1'bz;  // Controlled_Inverter controlled_inverter_2
  Pull_Resistor #(.pull(0)) pull_resistor_3 (.node(IRC));
  assign IRC = or_2_out ? ~CLK : 1'bz;  // Controlled_Inverter controlled_inverter_3
  Hex_Digit_Display hex_digit_display_6 (.value(LedData[11:8]));  // open: dp
  Hex_Digit_Display hex_digit_display_7 (.value(LedData[7:4]));  // open: dp
  // Probe on \总周期数 
  Hex_Digit_Display hex_digit_display_8 (.value(LedData[3:0]));  // open: dp
  or or_3 (IR1_t, IR1, IRA);
  or or_4 (IR2_t, IR2, IRB);
  or or_5 (IR3_t, IR3, IRC);
  D_Flip_Flop #(.trigger("high"), .Pre_Clr_Positions("LEGACY"), .NegatePresetClear("false"), .enable("true"), .NewFFLayout("false")) d_ff_1 (.Q(d_ff_1_q));  // open: clk, D, Qn, preset, en, reset
  // Probe on 13'hc
  Comparator #(.width(13), .mode("twosComplement")) comparator_6 (
    .a(CNT_num), .b(13'hc), .eq(comparator_6_eq), .lt(comparator_6_lt));  // open: gt
  Clock #(.highDuration(1), .lowDuration(1)) clock_1 (.out(clock_1_out));
  Counter #(.width(13), .max('h1fff), .ongoal("stay"), .trigger("rising"), .behavior("old")) counter_1 (
    .count(comparator_6_lt), .Q(CNT_num), .clk(clock_1_out));  // open: load, D, carry, clr, preset
  nand nand_1 (nand_1_out, d_ff_1_q, comparator_6_eq);
  assign CLK = nand_1_out ? clock_1_out : 1'bz;  // Controlled_Buffer controlled_buffer_1
  Pull_Resistor #(.pull(1)) pull_resistor_4 (.node(CLK));

  // Notes on the sheet:
  //   中断源
  //   中断等待指示
  //   总复位信号应将除ROM以外所有存储组件全部清零
  //   多级中断测试信号模拟器
  //   数码管输出
  //   数码管输出应该用寄存器锁存，否则显示数据只能一闪而过
  //   为方便自动评测，需要输出PC，IR，寄存器堆写如数据RDin
  //   RAM写使能MemWrite、RAM写入数据MDin等信号
  //   控制位
  //   暂停节拍，不能为0
  //   戳工具置1进入计数暂停模式，ctrl+k时钟自动运行到对应节拍暂停
  //   ctrl+k关闭时钟连续运行，将控制位置零，进入单步调试模式调试
  //   可计数暂停的时钟源
endmodule

module \封装正确性测试  (
);

  wire IR1, IR2, IR3, MemW, RegW;
  wire [31:0] EX_PC, ID_PC, IF_PC, IR, LED, MDin, MDinr, MEM_PC, PC, RDin, RDinr, WB_PC;

  \单周期RISC_V  \u_单周期risc_v_1  (
    .IR1(IR1), .IR2(IR2), .IR3(IR3), .RegWrite(RegW), .MemWrite(MemW), .PC(PC), .IR(IR), .RDin(RDin),
    .MDin(MDin), .LedData(LED));
  \气泡流水线  \u_气泡流水线_1  (
    .RegWrite(RegW), .MemWrite(MemW), .IF_PC(IF_PC), .ID_PC(ID_PC), .EX_PC(EX_PC), .M_PC(MEM_PC),
    .WB_PC(WB_PC), .RDin(RDinr), .MDin(MDinr), .LedData(LED));
  \单周期_单级中断  \u_单周期_单级中断_1  (
    .IR1(IR1), .IR2(IR2), .IR3(IR3), .RegWrite(RegW), .MemWrite(MemW), .PC(PC), .IR(IR), .RDin(RDin),
    .MDin(MDin), .LedData(LED));
  \理想流水线  \u_理想流水线_1  (
    .RegWrite(RegW), .MemWrite(MemW), .IF_PC(IF_PC), .ID_PC(ID_PC), .EX_PC(EX_PC), .M_PC(MEM_PC),
    .WB_PC(WB_PC), .RDin(RDinr), .MDin(MDinr), .LedData(LED));
  \重定向流水线  \u_重定向流水线_1  (
    .RegWrite(RegW), .MemWrite(MemW), .IF_PC(IF_PC), .ID_PC(ID_PC), .EX_PC(EX_PC), .M_PC(MEM_PC),
    .WB_PC(WB_PC), .RDin(RDinr), .MDin(MDinr), .LedData(LED));
  \单周期_多级中断  \u_单周期_多级中断_1  (
    .IR1(IR1), .IR2(IR2), .IR3(IR3), .RegWrite(RegW), .MemWrite(MemW), .PC(PC), .IR(IR), .RDin(RDin),
    .MDin(MDin), .LedData(LED));

  // Notes on the sheet:
  //   单周期封装测试
  //   气泡流水封装测试
  //   单周期+单级中断封装测试
  //   请检查上面封装有无位宽不匹配，引脚标签是否和连接的标签相对应，否则无法在educoder平台上正确测试
  //   理想流水封装测试
  //   重定向流水封装测试
  //   单周期+多级中断封装测试
endmodule
module \流水寄存器  (
  input  Beq,
  input  Bne,
  input  MemToReg,
  input  MemWrite,
  input  AluSrcB,
  input  RegWrite,
  input  halt,
  input  ecall,
  input  Jal,
  input  Jalr,
  input  URET,
  input  BLTU,
  input  [3:0] AluOP,
  input  [4:0] rd,
  input  [31:0] R1,
  input  [31:0] R2,
  input  [31:0] imm_1,
  input  [31:0] imm_2,
  input  [31:0] imm_3,
  input  [31:0] PC,
  input  [31:0] PC_4,
  input  [31:0] IR,
  input  [1:0] RS1_Forward,
  input  [1:0] RS2_Forward,
  input  halt_2,
  input  clk,
  input  reset,
  input  flush,
  output Beq_2,
  output Bne_2,
  output MemToReg_2,
  output MemWrite_2,
  output AluSrcB_2,
  output RegWrite_2,
  output halt_3,
  output ecall_2,
  output Jal_2,
  output Jalr_2,
  output URET_2,
  output BLTU_2,
  output [3:0] AluOP_2,
  output [4:0] rd_2,
  output [31:0] R1_2,
  output [31:0] R2_2,
  output [31:0] imm_1_2,
  output [31:0] imm_2_2,
  output [31:0] imm_3_2,
  output [31:0] PC_2,
  output [31:0] PC_4_2,
  output [31:0] IR_2,
  output [1:0] RS1_Forward_2,
  output [1:0] RS2_Forward_2
);

  wire multiplexer_1_out, multiplexer_2_out, multiplexer_3_out, multiplexer_4_out, multiplexer_5_out,
       multiplexer_6_out, multiplexer_7_out, multiplexer_8_out, multiplexer_9_out, multiplexer_10_out,
       multiplexer_11_out, multiplexer_12_out, not_1_out, or_1_out;
  wire [1:0] multiplexer_23_out, multiplexer_24_out;
  wire [3:0] multiplexer_13_out;
  wire [4:0] multiplexer_14_out;
  wire [31:0] multiplexer_15_out, multiplexer_16_out, multiplexer_17_out, multiplexer_18_out,
       multiplexer_19_out, multiplexer_20_out, multiplexer_21_out, multiplexer_22_out;

  Multiplexer #(.select(1), .width(1), .disabled("Z"), .enable("false")) multiplexer_1 (
    .in0(Beq), .in1(1'b0), .out(multiplexer_1_out), .sel(or_1_out));
  Multiplexer #(.select(1), .width(1), .disabled("Z"), .enable("false")) multiplexer_2 (
    .in0(Bne), .in1(1'b0), .out(multiplexer_2_out), .sel(or_1_out));
  Multiplexer #(.select(1), .width(1), .disabled("Z"), .enable("false")) multiplexer_3 (
    .in0(MemToReg), .in1(1'b0), .out(multiplexer_3_out), .sel(or_1_out));
  Multiplexer #(.select(1), .width(1), .disabled("Z"), .enable("false")) multiplexer_4 (
    .in0(MemWrite), .in1(1'b0), .out(multiplexer_4_out), .sel(or_1_out));
  Multiplexer #(.select(1), .width(1), .disabled("Z"), .enable("false")) multiplexer_5 (
    .in0(AluSrcB), .in1(1'b0), .out(multiplexer_5_out), .sel(or_1_out));
  Multiplexer #(.select(1), .width(1), .disabled("Z"), .enable("false")) multiplexer_6 (
    .in0(RegWrite), .in1(1'b0), .out(multiplexer_6_out), .sel(or_1_out));
  Multiplexer #(.select(1), .width(1), .disabled("Z"), .enable("false")) multiplexer_7 (
    .in0(halt), .in1(1'b0), .out(multiplexer_7_out), .sel(or_1_out));
  Multiplexer #(.select(1), .width(1), .disabled("Z"), .enable("false")) multiplexer_8 (
    .in0(ecall), .in1(1'b0), .out(multiplexer_8_out), .sel(or_1_out));
  Multiplexer #(.select(1), .width(1), .disabled("Z"), .enable("false")) multiplexer_9 (
    .in0(Jal), .in1(1'b0), .out(multiplexer_9_out), .sel(or_1_out));
  Multiplexer #(.select(1), .width(1), .disabled("Z"), .enable("false")) multiplexer_10 (
    .in0(Jalr), .in1(1'b0), .out(multiplexer_10_out), .sel(or_1_out));
  Multiplexer #(.select(1), .width(1), .disabled("Z"), .enable("false")) multiplexer_11 (
    .in0(URET), .in1(1'b0), .out(multiplexer_11_out), .sel(or_1_out));
  Multiplexer #(.select(1), .width(1), .disabled("Z"), .enable("false")) multiplexer_12 (
    .in0(BLTU), .in1(1'b0), .out(multiplexer_12_out), .sel(or_1_out));
  Multiplexer #(.select(1), .width(4), .disabled("Z"), .enable("false")) multiplexer_13 (
    .in0(AluOP), .in1(4'b0000), .out(multiplexer_13_out), .sel(or_1_out));
  Multiplexer #(.select(1), .width(5), .disabled("Z"), .enable("false")) multiplexer_14 (
    .in0(rd), .in1({5{1'b0}}), .out(multiplexer_14_out), .sel(or_1_out));
  Multiplexer #(.select(1), .width(32), .disabled("Z"), .enable("false")) multiplexer_15 (
    .in0(R1), .in1({32{1'b0}}), .out(multiplexer_15_out), .sel(or_1_out));
  Multiplexer #(.select(1), .width(32), .disabled("Z"), .enable("false")) multiplexer_16 (
    .in0(R2), .in1({32{1'b0}}), .out(multiplexer_16_out), .sel(or_1_out));
  Multiplexer #(.select(1), .width(32), .disabled("Z"), .enable("false")) multiplexer_17 (
    .in0(imm_1), .in1({32{1'b0}}), .out(multiplexer_17_out), .sel(or_1_out));
  Multiplexer #(.select(1), .width(32), .disabled("Z"), .enable("false")) multiplexer_18 (
    .in0(imm_2), .in1({32{1'b0}}), .out(multiplexer_18_out), .sel(or_1_out));
  Multiplexer #(.select(1), .width(32), .disabled("Z"), .enable("false")) multiplexer_19 (
    .in0(imm_3), .in1({32{1'b0}}), .out(multiplexer_19_out), .sel(or_1_out));
  Multiplexer #(.select(1), .width(32), .disabled("Z"), .enable("false")) multiplexer_20 (
    .in0(PC), .in1({32{1'b0}}), .out(multiplexer_20_out), .sel(or_1_out));
  Multiplexer #(.select(1), .width(32), .disabled("Z"), .enable("false")) multiplexer_21 (
    .in0(PC_4), .in1({32{1'b0}}), .out(multiplexer_21_out), .sel(or_1_out));
  Multiplexer #(.select(1), .width(32), .disabled("Z"), .enable("false")) multiplexer_22 (
    .in0(IR), .in1({32{1'b0}}), .out(multiplexer_22_out), .sel(or_1_out));
  Multiplexer #(.select(1), .width(2), .disabled("Z"), .enable("false")) multiplexer_23 (
    .in0(RS1_Forward), .in1(2'b00), .out(multiplexer_23_out), .sel(or_1_out));
  Multiplexer #(.select(1), .width(2), .disabled("Z"), .enable("false")) multiplexer_24 (
    .in0(RS2_Forward), .in1(2'b00), .out(multiplexer_24_out), .sel(or_1_out));
  or or_1 (or_1_out, reset, flush);
  not not_1 (not_1_out, halt_2);
  Register #(.width(1), .trigger("rising"), .Select("low")) register_1 (
    .D(multiplexer_1_out), .en(not_1_out), .Q(Beq_2), .clk(clk));  // open: clr
  Register #(.width(1), .trigger("rising"), .Select("low")) register_2 (
    .D(multiplexer_2_out), .en(not_1_out), .Q(Bne_2), .clk(clk));  // open: clr
  Register #(.width(1), .trigger("rising"), .Select("low")) register_3 (
    .D(multiplexer_3_out), .en(not_1_out), .Q(MemToReg_2), .clk(clk));  // open: clr
  Register #(.width(1), .trigger("rising"), .Select("low")) register_4 (
    .D(multiplexer_4_out), .en(not_1_out), .Q(MemWrite_2), .clk(clk));  // open: clr
  Register #(.width(1), .trigger("rising"), .Select("low")) register_5 (
    .D(multiplexer_5_out), .en(not_1_out), .Q(AluSrcB_2), .clk(clk));  // open: clr
  Register #(.width(1), .trigger("rising"), .Select("low")) register_6 (
    .D(multiplexer_6_out), .en(not_1_out), .Q(RegWrite_2), .clk(clk));  // open: clr
  Register #(.width(1), .trigger("rising"), .Select("low")) register_7 (
    .D(multiplexer_7_out), .en(not_1_out), .Q(halt_3), .clk(clk));  // open: clr
  Register #(.width(1), .trigger("rising"), .Select("low")) register_8 (
    .D(multiplexer_8_out), .en(not_1_out), .Q(ecall_2), .clk(clk));  // open: clr
  Register #(.width(1), .trigger("rising"), .Select("low")) register_9 (
    .D(multiplexer_9_out), .en(not_1_out), .Q(Jal_2), .clk(clk));  // open: clr
  Register #(.width(1), .trigger("rising"), .Select("low")) register_10 (
    .D(multiplexer_10_out), .en(not_1_out), .Q(Jalr_2), .clk(clk));  // open: clr
  Register #(.width(1), .trigger("rising"), .Select("low")) register_11 (
    .D(multiplexer_11_out), .en(not_1_out), .Q(URET_2), .clk(clk));  // open: clr
  Register #(.width(1), .trigger("rising"), .Select("low")) register_12 (
    .D(multiplexer_12_out), .en(not_1_out), .Q(BLTU_2), .clk(clk));  // open: clr
  Register #(.width(4), .trigger("rising"), .Select("low")) register_13 (
    .D(multiplexer_13_out), .en(not_1_out), .Q(AluOP_2), .clk(clk));  // open: clr
  Register #(.width(5), .trigger("rising"), .Select("low")) register_14 (
    .D(multiplexer_14_out), .en(not_1_out), .Q(rd_2), .clk(clk));  // open: clr
  Register #(.width(32), .trigger("rising"), .Select("low")) register_15 (
    .D(multiplexer_15_out), .en(not_1_out), .Q(R1_2), .clk(clk));  // open: clr
  Register #(.width(32), .trigger("rising"), .Select("low")) register_16 (
    .D(multiplexer_16_out), .en(not_1_out), .Q(R2_2), .clk(clk));  // open: clr
  Register #(.width(32), .trigger("rising"), .Select("low")) register_17 (
    .D(multiplexer_17_out), .en(not_1_out), .Q(imm_1_2), .clk(clk));  // open: clr
  Register #(.width(32), .trigger("rising"), .Select("low")) register_18 (
    .D(multiplexer_18_out), .en(not_1_out), .Q(imm_2_2), .clk(clk));  // open: clr
  Register #(.width(32), .trigger("rising"), .Select("low")) register_19 (
    .D(multiplexer_19_out), .en(not_1_out), .Q(imm_3_2), .clk(clk));  // open: clr
  Register #(.width(32), .trigger("rising"), .Select("low")) register_20 (
    .D(multiplexer_20_out), .en(not_1_out), .Q(PC_2), .clk(clk));  // open: clr
  Register #(.width(32), .trigger("rising"), .Select("low")) register_21 (
    .D(multiplexer_21_out), .en(not_1_out), .Q(PC_4_2), .clk(clk));  // open: clr
  Register #(.width(32), .trigger("rising"), .Select("low")) register_22 (
    .D(multiplexer_22_out), .en(not_1_out), .Q(IR_2), .clk(clk));  // open: clr
  Register #(.width(2), .trigger("rising"), .Select("low")) register_23 (
    .D(multiplexer_23_out), .en(not_1_out), .Q(RS1_Forward_2), .clk(clk));  // open: clr
  Register #(.width(2), .trigger("rising"), .Select("low")) register_24 (
    .D(multiplexer_24_out), .en(not_1_out), .Q(RS2_Forward_2), .clk(clk));  // open: clr
endmodule

module \源寄存器使用情况  (
  input  [4:0] OP,
  input  [4:0] Funct,
  output rs1_used,
  output rs2_used
);

  wire and_1_out, and_2_out, and_3_out, and_4_out, and_5_out, and_6_out, and_7_out, and_8_out, and_9_out,
       and_10_out, and_11_out, and_12_out, and_13_out, and_14_out, and_15_out, and_16_out, and_17_out,
       and_18_out, and_19_out, and_20_out, and_21_out, and_22_out, and_23_out, and_24_out, and_25_out,
       and_26_out, and_27_out, and_28_out, and_29_out, and_30_out, and_31_out, and_32_out, and_33_out,
       and_34_out, and_35_out, and_36_out, and_37_out, not_1_out, not_2_out, not_3_out, not_4_out, not_5_out,
       not_6_out, not_7_out, not_8_out, not_9_out, not_10_out, not_11_out, not_12_out, not_13_out,
       not_14_out, not_15_out, not_16_out, not_17_out, not_18_out, not_19_out, not_20_out, not_21_out,
       not_22_out, not_23_out, not_24_out, not_25_out, not_26_out, not_27_out, not_28_out, not_29_out,
       not_30_out, not_31_out, not_32_out, not_33_out, not_34_out, not_35_out, not_36_out, not_37_out,
       not_38_out, not_39_out, not_40_out, not_41_out, not_42_out, not_43_out, not_44_out, not_45_out,
       not_46_out, not_47_out, not_48_out, not_49_out, not_50_out, not_51_out, not_52_out, not_53_out,
       not_54_out, not_55_out, not_56_out, not_57_out, not_58_out, not_59_out, not_60_out, not_61_out,
       not_62_out, not_63_out, not_64_out, not_65_out, not_66_out, not_67_out, not_68_out, not_69_out,
       not_70_out, not_71_out, not_72_out, not_73_out, not_74_out, not_75_out, not_76_out, not_77_out,
       not_78_out, not_79_out, not_80_out, not_81_out, not_82_out, not_83_out, not_84_out, not_85_out,
       not_86_out, not_87_out, not_88_out, not_89_out, not_90_out, not_91_out, not_92_out, not_93_out,
       not_94_out, not_95_out, not_96_out, not_97_out, not_98_out, not_99_out, not_100_out, not_101_out,
       not_102_out, not_103_out, not_104_out, not_105_out, not_106_out, not_107_out, not_108_out,
       not_109_out, not_110_out, not_111_out, not_112_out, not_113_out, not_114_out, not_115_out,
       not_116_out, not_117_out, not_118_out, not_119_out, not_120_out, not_121_out, not_122_out,
       not_123_out, not_124_out, not_125_out, not_126_out, not_127_out, not_128_out, not_129_out,
       not_130_out, not_131_out, not_132_out, not_133_out, not_134_out, not_135_out, not_136_out,
       not_137_out, not_138_out, not_139_out, not_140_out, not_141_out, not_142_out, not_143_out,
       not_144_out, not_145_out, not_146_out, not_147_out, not_148_out, not_149_out, not_150_out,
       not_151_out, not_152_out, not_153_out, not_154_out, not_155_out, not_156_out, not_157_out,
       not_158_out, not_159_out, not_160_out, not_161_out, not_162_out, not_163_out, not_164_out,
       not_165_out, not_166_out, not_167_out, not_168_out, not_169_out, not_170_out, not_171_out,
       not_172_out, not_173_out, not_174_out, not_175_out, not_176_out, not_177_out, not_178_out,
       not_179_out, not_180_out, not_181_out, not_182_out, not_183_out, not_184_out, not_185_out,
       not_186_out, not_187_out, not_188_out, not_189_out, not_190_out, not_191_out, not_192_out,
       not_193_out, not_194_out, not_195_out, not_196_out, not_197_out, not_198_out, not_199_out,
       not_200_out, not_201_out, not_202_out, not_203_out, not_204_out, not_205_out, not_206_out,
       not_207_out, not_208_out, not_209_out, not_210_out, not_211_out, not_212_out, not_213_out,
       not_214_out, not_215_out, not_216_out, not_217_out, not_218_out, not_219_out, not_220_out, not_221_out;

  not not_1 (not_1_out, Funct[4]);
  not not_2 (not_2_out, Funct[3]);
  not not_3 (not_3_out, Funct[2]);
  not not_4 (not_4_out, Funct[1]);
  not not_5 (not_5_out, Funct[0]);
  not not_6 (not_6_out, OP[4]);
  not not_7 (not_7_out, OP[1]);
  not not_8 (not_8_out, OP[0]);
  not not_9 (not_9_out, Funct[3]);
  not not_10 (not_10_out, Funct[2]);
  not not_11 (not_11_out, Funct[1]);
  not not_12 (not_12_out, Funct[0]);
  not not_13 (not_13_out, OP[4]);
  not not_14 (not_14_out, OP[1]);
  not not_15 (not_15_out, OP[0]);
  not not_16 (not_16_out, Funct[4]);
  not not_17 (not_17_out, Funct[3]);
  not not_18 (not_18_out, OP[4]);
  not not_19 (not_19_out, OP[1]);
  not not_20 (not_20_out, OP[0]);
  not not_21 (not_21_out, Funct[4]);
  not not_22 (not_22_out, Funct[3]);
  not not_23 (not_23_out, Funct[0]);
  not not_24 (not_24_out, OP[4]);
  not not_25 (not_25_out, OP[1]);
  not not_26 (not_26_out, OP[0]);
  not not_27 (not_27_out, Funct[4]);
  not not_28 (not_28_out, Funct[3]);
  not not_29 (not_29_out, Funct[2]);
  not not_30 (not_30_out, Funct[0]);
  not not_31 (not_31_out, OP[4]);
  not not_32 (not_32_out, OP[1]);
  not not_33 (not_33_out, OP[0]);
  not not_34 (not_34_out, Funct[4]);
  not not_35 (not_35_out, Funct[3]);
  not not_36 (not_36_out, Funct[2]);
  not not_37 (not_37_out, OP[4]);
  not not_38 (not_38_out, OP[1]);
  not not_39 (not_39_out, OP[0]);
  not not_40 (not_40_out, Funct[2]);
  not not_41 (not_41_out, Funct[1]);
  not not_42 (not_42_out, Funct[0]);
  not not_43 (not_43_out, OP[4]);
  not not_44 (not_44_out, OP[3]);
  not not_45 (not_45_out, OP[1]);
  not not_46 (not_46_out, OP[0]);
  not not_47 (not_47_out, OP[4]);
  not not_48 (not_48_out, OP[3]);
  not not_49 (not_49_out, OP[1]);
  not not_50 (not_50_out, OP[0]);
  not not_51 (not_51_out, Funct[0]);
  not not_52 (not_52_out, OP[4]);
  not not_53 (not_53_out, OP[3]);
  not not_54 (not_54_out, OP[1]);
  not not_55 (not_55_out, OP[0]);
  not not_56 (not_56_out, Funct[1]);
  not not_57 (not_57_out, Funct[0]);
  not not_58 (not_58_out, OP[4]);
  not not_59 (not_59_out, OP[3]);
  not not_60 (not_60_out, OP[1]);
  not not_61 (not_61_out, OP[0]);
  not not_62 (not_62_out, Funct[2]);
  not not_63 (not_63_out, Funct[0]);
  not not_64 (not_64_out, OP[4]);
  not not_65 (not_65_out, OP[3]);
  not not_66 (not_66_out, OP[1]);
  not not_67 (not_67_out, OP[0]);
  not not_68 (not_68_out, Funct[4]);
  not not_69 (not_69_out, Funct[3]);
  not not_70 (not_70_out, Funct[2]);
  not not_71 (not_71_out, Funct[1]);
  not not_72 (not_72_out, OP[4]);
  not not_73 (not_73_out, OP[3]);
  not not_74 (not_74_out, OP[1]);
  not not_75 (not_75_out, OP[0]);
  not not_76 (not_76_out, Funct[4]);
  not not_77 (not_77_out, Funct[3]);
  not not_78 (not_78_out, Funct[1]);
  not not_79 (not_79_out, OP[4]);
  not not_80 (not_80_out, OP[3]);
  not not_81 (not_81_out, OP[1]);
  not not_82 (not_82_out, OP[0]);
  not not_83 (not_83_out, Funct[3]);
  not not_84 (not_84_out, Funct[1]);
  not not_85 (not_85_out, OP[4]);
  not not_86 (not_86_out, OP[3]);
  not not_87 (not_87_out, OP[1]);
  not not_88 (not_88_out, OP[0]);
  not not_89 (not_89_out, Funct[2]);
  not not_90 (not_90_out, Funct[0]);
  not not_91 (not_91_out, OP[4]);
  not not_92 (not_92_out, OP[3]);
  not not_93 (not_93_out, OP[2]);
  not not_94 (not_94_out, OP[1]);
  not not_95 (not_95_out, OP[0]);
  not not_96 (not_96_out, Funct[2]);
  not not_97 (not_97_out, Funct[0]);
  not not_98 (not_98_out, OP[4]);
  not not_99 (not_99_out, OP[2]);
  not not_100 (not_100_out, OP[1]);
  not not_101 (not_101_out, OP[0]);
  not not_102 (not_102_out, Funct[4]);
  not not_103 (not_103_out, Funct[3]);
  not not_104 (not_104_out, Funct[2]);
  not not_105 (not_105_out, Funct[1]);
  not not_106 (not_106_out, Funct[0]);
  not not_107 (not_107_out, OP[1]);
  not not_108 (not_108_out, OP[0]);
  not not_109 (not_109_out, Funct[2]);
  not not_110 (not_110_out, Funct[1]);
  not not_111 (not_111_out, Funct[0]);
  not not_112 (not_112_out, OP[2]);
  not not_113 (not_113_out, OP[1]);
  not not_114 (not_114_out, OP[0]);
  not not_115 (not_115_out, Funct[2]);
  not not_116 (not_116_out, Funct[1]);
  not not_117 (not_117_out, OP[2]);
  not not_118 (not_118_out, OP[1]);
  not not_119 (not_119_out, OP[0]);
  not not_120 (not_120_out, Funct[2]);
  not not_121 (not_121_out, Funct[1]);
  not not_122 (not_122_out, Funct[0]);
  not not_123 (not_123_out, OP[2]);
  not not_124 (not_124_out, OP[1]);
  not not_125 (not_125_out, Funct[4]);
  not not_126 (not_126_out, Funct[3]);
  not not_127 (not_127_out, Funct[1]);
  not not_128 (not_128_out, OP[4]);
  not not_129 (not_129_out, OP[1]);
  not not_130 (not_130_out, OP[0]);
  not not_131 (not_131_out, OP[4]);
  not not_132 (not_132_out, OP[1]);
  not not_133 (not_133_out, Funct[2]);
  not not_134 (not_134_out, Funct[1]);
  not not_135 (not_135_out, OP[4]);
  not not_136 (not_136_out, OP[2]);
  not not_137 (not_137_out, OP[1]);
  not not_138 (not_138_out, OP[0]);
  not not_139 (not_139_out, Funct[0]);
  not not_140 (not_140_out, OP[2]);
  not not_141 (not_141_out, OP[1]);
  not not_142 (not_142_out, OP[0]);
  not not_143 (not_143_out, Funct[4]);
  not not_144 (not_144_out, Funct[3]);
  not not_145 (not_145_out, Funct[2]);
  not not_146 (not_146_out, Funct[1]);
  not not_147 (not_147_out, Funct[0]);
  not not_148 (not_148_out, OP[4]);
  not not_149 (not_149_out, OP[1]);
  not not_150 (not_150_out, OP[0]);
  not not_151 (not_151_out, Funct[3]);
  not not_152 (not_152_out, Funct[2]);
  not not_153 (not_153_out, Funct[1]);
  not not_154 (not_154_out, Funct[0]);
  not not_155 (not_155_out, OP[4]);
  not not_156 (not_156_out, OP[1]);
  not not_157 (not_157_out, OP[0]);
  not not_158 (not_158_out, Funct[4]);
  not not_159 (not_159_out, Funct[3]);
  not not_160 (not_160_out, OP[4]);
  not not_161 (not_161_out, OP[1]);
  not not_162 (not_162_out, OP[0]);
  not not_163 (not_163_out, Funct[4]);
  not not_164 (not_164_out, Funct[3]);
  not not_165 (not_165_out, Funct[0]);
  not not_166 (not_166_out, OP[4]);
  not not_167 (not_167_out, OP[1]);
  not not_168 (not_168_out, OP[0]);
  not not_169 (not_169_out, Funct[4]);
  not not_170 (not_170_out, Funct[3]);
  not not_171 (not_171_out, Funct[2]);
  not not_172 (not_172_out, Funct[0]);
  not not_173 (not_173_out, OP[4]);
  not not_174 (not_174_out, OP[1]);
  not not_175 (not_175_out, OP[0]);
  not not_176 (not_176_out, Funct[4]);
  not not_177 (not_177_out, Funct[3]);
  not not_178 (not_178_out, Funct[2]);
  not not_179 (not_179_out, OP[4]);
  not not_180 (not_180_out, OP[1]);
  not not_181 (not_181_out, OP[0]);
  not not_182 (not_182_out, Funct[2]);
  not not_183 (not_183_out, Funct[0]);
  not not_184 (not_184_out, OP[4]);
  not not_185 (not_185_out, OP[2]);
  not not_186 (not_186_out, OP[1]);
  not not_187 (not_187_out, OP[0]);
  not not_188 (not_188_out, Funct[4]);
  not not_189 (not_189_out, Funct[3]);
  not not_190 (not_190_out, Funct[2]);
  not not_191 (not_191_out, Funct[1]);
  not not_192 (not_192_out, Funct[0]);
  not not_193 (not_193_out, OP[1]);
  not not_194 (not_194_out, OP[0]);
  not not_195 (not_195_out, Funct[2]);
  not not_196 (not_196_out, Funct[1]);
  not not_197 (not_197_out, Funct[0]);
  not not_198 (not_198_out, OP[2]);
  not not_199 (not_199_out, OP[1]);
  not not_200 (not_200_out, OP[0]);
  not not_201 (not_201_out, Funct[2]);
  not not_202 (not_202_out, Funct[1]);
  not not_203 (not_203_out, OP[2]);
  not not_204 (not_204_out, OP[1]);
  not not_205 (not_205_out, OP[0]);
  not not_206 (not_206_out, Funct[4]);
  not not_207 (not_207_out, Funct[3]);
  not not_208 (not_208_out, Funct[1]);
  not not_209 (not_209_out, OP[4]);
  not not_210 (not_210_out, OP[1]);
  not not_211 (not_211_out, OP[0]);
  not not_212 (not_212_out, Funct[2]);
  not not_213 (not_213_out, Funct[1]);
  not not_214 (not_214_out, OP[4]);
  not not_215 (not_215_out, OP[2]);
  not not_216 (not_216_out, OP[1]);
  not not_217 (not_217_out, OP[0]);
  not not_218 (not_218_out, Funct[0]);
  not not_219 (not_219_out, OP[2]);
  not not_220 (not_220_out, OP[1]);
  not not_221 (not_221_out, OP[0]);
  and and_1 (and_1_out, not_1_out, not_2_out, not_3_out, not_4_out, not_5_out, not_6_out, OP[3], OP[2], not_7_out, not_8_out);
  and and_2 (and_2_out, Funct[4], not_9_out, not_10_out, not_11_out, not_12_out, not_13_out, OP[3], OP[2], not_14_out, not_15_out);
  and and_3 (and_3_out, not_16_out, not_17_out, Funct[2], Funct[1], Funct[0], not_18_out, OP[3], OP[2], not_19_out, not_20_out);
  and and_4 (and_4_out, not_21_out, not_22_out, Funct[2], Funct[1], not_23_out, not_24_out, OP[3], OP[2], not_25_out, not_26_out);
  and and_5 (and_5_out, not_27_out, not_28_out, not_29_out, Funct[1], not_30_out, not_31_out, OP[3], OP[2], not_32_out, not_33_out);
  and and_6 (and_6_out, not_34_out, not_35_out, not_36_out, Funct[1], Funct[0], not_37_out, OP[3], OP[2], not_38_out, not_39_out);
  and and_7 (and_7_out, not_40_out, not_41_out, not_42_out, not_43_out, not_44_out, OP[2], not_45_out, not_46_out);
  and and_8 (and_8_out, Funct[2], Funct[1], Funct[0], not_47_out, not_48_out, OP[2], not_49_out, not_50_out);
  and and_9 (and_9_out, Funct[2], Funct[1], not_51_out, not_52_out, not_53_out, OP[2], not_54_out, not_55_out);
  and and_10 (and_10_out, Funct[2], not_56_out, not_57_out, not_58_out, not_59_out, OP[2], not_60_out, not_61_out);
  and and_11 (and_11_out, not_62_out, Funct[1], not_63_out, not_64_out, not_65_out, OP[2], not_66_out, not_67_out);
  and and_12 (and_12_out, not_68_out, not_69_out, not_70_out, not_71_out, Funct[0], not_72_out, not_73_out, OP[2], not_74_out, not_75_out);
  and and_13 (and_13_out, not_76_out, not_77_out, Funct[2], not_78_out, Funct[0], not_79_out, not_80_out, OP[2], not_81_out, not_82_out);
  and and_14 (and_14_out, Funct[4], not_83_out, Funct[2], not_84_out, Funct[0], not_85_out, not_86_out, OP[2], not_87_out, not_88_out);
  and and_15 (and_15_out, not_89_out, Funct[1], not_90_out, not_91_out, not_92_out, not_93_out, not_94_out, not_95_out);
  and and_16 (and_16_out, not_96_out, Funct[1], not_97_out, not_98_out, OP[3], not_99_out, not_100_out, not_101_out);
  and and_17 (and_17_out, not_102_out, not_103_out, not_104_out, not_105_out, not_106_out, OP[4], OP[3], OP[2], not_107_out, not_108_out);
  and and_18 (and_18_out, not_109_out, not_110_out, not_111_out, OP[4], OP[3], not_112_out, not_113_out, not_114_out);
  and and_19 (and_19_out, not_115_out, not_116_out, Funct[0], OP[4], OP[3], not_117_out, not_118_out, not_119_out);
  and and_20 (and_20_out, not_120_out, not_121_out, not_122_out, OP[4], OP[3], not_123_out, not_124_out, OP[0]);
  and and_21 (and_21_out, not_125_out, not_126_out, Funct[2], not_127_out, Funct[0], not_128_out, OP[3], OP[2], not_129_out, not_130_out);
  and and_22 (and_22_out, not_131_out, OP[3], OP[2], not_132_out, OP[0]);
  and and_23 (and_23_out, not_133_out, not_134_out, Funct[0], not_135_out, OP[3], not_136_out, not_137_out, not_138_out);
  and and_24 (and_24_out, Funct[2], Funct[1], not_139_out, OP[4], OP[3], not_140_out, not_141_out, not_142_out);
  and and_25 (and_25_out, not_143_out, not_144_out, not_145_out, not_146_out, not_147_out, not_148_out, OP[3], OP[2], not_149_out, not_150_out);
  and and_26 (and_26_out, Funct[4], not_151_out, not_152_out, not_153_out, not_154_out, not_155_out, OP[3], OP[2], not_156_out, not_157_out);
  and and_27 (and_27_out, not_158_out, not_159_out, Funct[2], Funct[1], Funct[0], not_160_out, OP[3], OP[2], not_161_out, not_162_out);
  and and_28 (and_28_out, not_163_out, not_164_out, Funct[2], Funct[1], not_165_out, not_166_out, OP[3], OP[2], not_167_out, not_168_out);
  and and_29 (and_29_out, not_169_out, not_170_out, not_171_out, Funct[1], not_172_out, not_173_out, OP[3], OP[2], not_174_out, not_175_out);
  and and_30 (and_30_out, not_176_out, not_177_out, not_178_out, Funct[1], Funct[0], not_179_out, OP[3], OP[2], not_180_out, not_181_out);
  and and_31 (and_31_out, not_182_out, Funct[1], not_183_out, not_184_out, OP[3], not_185_out, not_186_out, not_187_out);
  and and_32 (and_32_out, not_188_out, not_189_out, not_190_out, not_191_out, not_192_out, OP[4], OP[3], OP[2], not_193_out, not_194_out);
  and and_33 (and_33_out, not_195_out, not_196_out, not_197_out, OP[4], OP[3], not_198_out, not_199_out, not_200_out);
  and and_34 (and_34_out, not_201_out, not_202_out, Funct[0], OP[4], OP[3], not_203_out, not_204_out, not_205_out);
  and and_35 (and_35_out, not_206_out, not_207_out, Funct[2], not_208_out, Funct[0], not_209_out, OP[3], OP[2], not_210_out, not_211_out);
  and and_36 (and_36_out, not_212_out, not_213_out, Funct[0], not_214_out, OP[3], not_215_out, not_216_out, not_217_out);
  and and_37 (and_37_out, Funct[2], Funct[1], not_218_out, OP[4], OP[3], not_219_out, not_220_out, not_221_out);
  or or_1 (rs2_used, and_25_out, and_26_out, and_27_out, and_28_out, and_29_out, and_30_out, and_31_out, and_32_out, and_33_out, and_34_out, and_35_out, and_36_out, and_37_out);
  or or_2 (rs1_used, and_1_out, and_2_out, and_3_out, and_4_out, and_5_out, and_6_out, and_7_out, and_8_out, and_9_out, and_10_out, and_11_out, and_12_out, and_13_out, and_14_out, and_15_out, and_16_out, and_17_out, and_18_out, and_19_out, and_20_out, and_21_out, and_22_out, and_23_out, and_24_out);
endmodule

module \数据相关检测  (
  input  [4:0] rs1,
  input  [4:0] rs2,
  input  rs1_used,
  input  EX_RegWrite,
  input  [4:0] EX_rd,
  input  rs2_used,
  input  MEM_RegWrite,
  input  [4:0] MEM_rd,
  input  EX_MemToReg,
  output [1:0] rs1Fwd,
  output DataCorrelate,
  output [1:0] rs2Fwd,
  output LoadUse
);

  wire and_1_out, and_2_out, and_3_out, and_4_out, and_5_out, and_6_out, and_7_out, and_8_out, and_9_out,
       and_10_out, and_11_out, and_12_out, and_14_out, and_16_out, and_17_out, and_18_out, comparator_1_eq,
       comparator_2_eq, comparator_3_eq, comparator_4_eq, comparator_5_eq, comparator_6_eq, comparator_7_eq,
       comparator_8_eq, comparator_9_eq, comparator_10_eq, comparator_11_eq, comparator_12_eq, not_1_out,
       not_2_out, not_3_out, not_4_out, not_5_out, not_6_out, not_7_out, not_8_out;

  Comparator #(.width(5), .mode("twosComplement")) comparator_1 (
    .a(rs1), .b(EX_rd), .eq(comparator_1_eq));  // open: gt, lt
  Comparator #(.width(5), .mode("twosComplement")) comparator_2 (
    .a(rs1), .b(MEM_rd), .eq(comparator_2_eq));  // open: gt, lt
  Comparator #(.width(5), .mode("twosComplement")) comparator_3 (
    .a(rs2), .b(EX_rd), .eq(comparator_3_eq));  // open: gt, lt
  Comparator #(.width(5), .mode("twosComplement")) comparator_4 (
    .a(rs2), .b(MEM_rd), .eq(comparator_4_eq));  // open: gt, lt
  Comparator #(.width(5), .mode("twosComplement")) comparator_5 (
    .a(rs1), .b(EX_rd), .eq(comparator_5_eq));  // open: gt, lt
  Comparator #(.width(5), .mode("twosComplement")) comparator_6 (
    .a(rs2), .b(EX_rd), .eq(comparator_6_eq));  // open: gt, lt
  not not_1 (not_1_out, comparator_7_eq);
  Comparator #(.width(5), .mode("twosComplement")) comparator_7 (
    .a({5{1'b0}}), .b(rs1), .eq(comparator_7_eq));  // open: gt, lt
  and and_1 (and_1_out, comparator_1_eq, EX_RegWrite);
  Comparator #(.width(5), .mode("twosComplement")) comparator_8 (
    .a({5{1'b0}}), .b(rs1), .eq(comparator_8_eq));  // open: gt, lt
  not not_2 (not_2_out, comparator_8_eq);
  and and_2 (and_2_out, comparator_2_eq, MEM_RegWrite);
  not not_3 (not_3_out, comparator_9_eq);
  Comparator #(.width(5), .mode("twosComplement")) comparator_9 (
    .a({5{1'b0}}), .b(rs2), .eq(comparator_9_eq));  // open: gt, lt
  and and_3 (and_3_out, comparator_3_eq, EX_RegWrite);
  not not_4 (not_4_out, comparator_10_eq);
  Comparator #(.width(5), .mode("twosComplement")) comparator_10 (
    .a({5{1'b0}}), .b(rs2), .eq(comparator_10_eq));  // open: gt, lt
  and and_4 (and_4_out, comparator_4_eq, MEM_RegWrite);
  not not_5 (not_5_out, comparator_11_eq);
  Comparator #(.width(5), .mode("twosComplement")) comparator_11 (
    .a({5{1'b0}}), .b(rs1), .eq(comparator_11_eq));  // open: gt, lt
  and and_5 (and_5_out, comparator_5_eq, EX_MemToReg);
  not not_6 (not_6_out, comparator_12_eq);
  Comparator #(.width(5), .mode("twosComplement")) comparator_12 (
    .a({5{1'b0}}), .b(rs2), .eq(comparator_12_eq));  // open: gt, lt
  and and_6 (and_6_out, comparator_6_eq, EX_MemToReg);
  and and_7 (and_7_out, not_1_out, and_1_out);
  and and_8 (and_8_out, not_2_out, and_2_out);
  and and_9 (and_9_out, not_3_out, and_3_out);
  and and_10 (and_10_out, not_4_out, and_4_out);
  and and_11 (and_11_out, not_5_out, and_5_out);
  and and_12 (and_12_out, not_6_out, and_6_out);
  and and_13 (rs1Fwd[0], and_7_out, rs1_used);
  and and_14 (and_14_out, and_8_out, rs1_used);
  and and_15 (rs2Fwd[0], and_9_out, rs2_used);
  and and_16 (and_16_out, and_10_out, rs2_used);
  and and_17 (and_17_out, and_11_out, rs1_used);
  and and_18 (and_18_out, and_12_out, rs2_used);
  not not_7 (not_7_out, rs1Fwd[0]);
  and and_19 (rs1Fwd[1], not_7_out, and_14_out);
  or or_1 (DataCorrelate, rs1Fwd[0], and_14_out, rs2Fwd[0], and_16_out);
  not not_8 (not_8_out, rs2Fwd[0]);
  and and_20 (rs2Fwd[1], not_8_out, and_16_out);
  or or_2 (LoadUse, and_17_out, and_18_out);
endmodule
